// Logisim project gates_diagrams.circ as structural Verilog: 1 circuit, main circuit main
module main (
  input  in,
  input  in_2,
  input  sel,
  input  a,
  input  b,
  input  a_0,
  input  a_1,
  input  a_2,
  input  a_3,
  input  a_4,
  input  b_4,
  input  b_0,
  input  b_1,
  input  b_2,
  input  b_3,
  input  a_5,
  input  b_5,
  input  in_18,
  input  in_19,
  input  in_20,
  input  a_6,
  input  in_22,
  input  in_23,
  input  b_6,
  input  in_25,
  input  sel_2,
  output a_7,
  output out,
  output b_7,
  output out_4,
  output out_0,
  output out_5,
  output out_1,
  output out_2,
  output out_3,
  output out_6,
  output out_37,
  output out_7
);

  wire and_1_out, and_2_out, multiplexer_1_out, multiplexer_2_out, nand_2_out, nand_4_out, not_1_out,
       not_2_out, not_3_out, not_5_out, or_1_out;

  not not_1 (not_1_out, a_4);
  not not_2 (not_2_out, b_4);
  not not_3 (not_3_out, sel_2);
  nand nand_1 (out, in_2, in_2);
  not not_4 (out_4, nand_2_out);
  nand nand_2 (nand_2_out, a, b);
  nand nand_3 (out_5, not_1_out, not_2_out);
  or or_1 (or_1_out, a_5, b_5);
  nand nand_4 (nand_4_out, a_5, b_5);
  and and_1 (and_1_out, a_6, not_3_out);
  and and_2 (and_2_out, b_6, sel_2);
  and and_3 (out_6, or_1_out, nand_4_out);
  or or_2 (out_7, and_1_out, and_2_out);
  and and_4 (a_7, in, not_5_out);
  not not_5 (not_5_out, sel);
  and and_5 (b_7, in, sel);
  Multiplexer #(.enable("false")) multiplexer_1 (.in0(in_18), .in1(in_19), .out(multiplexer_1_out), .sel(in_23));
  Multiplexer #(.enable("false")) multiplexer_2 (.in0(in_20), .in1(in_22), .out(multiplexer_2_out), .sel(in_23));
  and and_6 (out_0, a_0, b_0);
  and and_7 (out_1, a_1, b_1);
  and and_8 (out_2, a_2, b_2);
  and and_9 (out_3, a_3, b_3);
  Multiplexer #(.enable("false")) multiplexer_3 (
    .in0(multiplexer_1_out), .in1(multiplexer_2_out), .out(out_37), .sel(in_25));

  // Notes on the sheet:
  //   NOT Gate
  //   AND Gate
  //   OR Gate
  //   XOR Gate
  //   MUX Gate
  //   DMUX Gate
  //   4-bit AND Gate
  //   4-way MUX Gate
endmodule
