// Logisim project 16-bit ALU.circ as structural Verilog: 1 circuit, main circuit main
module main (
  input  X15,
  input  X14,
  input  X13,
  input  X12,
  input  X11,
  input  X10,
  input  X9,
  input  ZX,
  input  NX,
  input  ZY,
  input  NY,
  input  F,
  input  NO,
  input  X8,
  input  X7,
  input  X6,
  input  X5,
  input  X4,
  input  X3,
  input  X2,
  input  X1,
  input  X0,
  input  Y15,
  input  Y14,
  input  Y13,
  input  Y12,
  input  Y11,
  input  Y10,
  input  Y9,
  input  Y8,
  input  Y7,
  input  Y6,
  input  Y5,
  input  Y4,
  input  Y3,
  input  Y2,
  input  Y1,
  input  Y0,
  output O15,
  output O14,
  output O13,
  output O12,
  output O11,
  output O10,
  output O9,
  output O8,
  output O7,
  output O6,
  output O5,
  output O4,
  output O3,
  output O2,
  output O1,
  output O0,
  output ZR,
  output NG
);

  wire and_1_out, and_2_out, and_3_out, and_4_out, and_5_out, and_6_out, and_7_out, and_8_out, and_9_out,
       and_10_out, and_11_out, and_12_out, and_13_out, and_14_out, and_15_out, and_16_out, and_17_out,
       and_18_out, and_19_out, and_20_out, and_21_out, and_22_out, and_23_out, and_24_out, and_25_out,
       and_26_out, and_27_out, and_28_out, and_29_out, and_30_out, and_31_out, and_32_out, and_33_out,
       and_34_out, and_35_out, and_36_out, and_37_out, and_38_out, and_39_out, and_40_out, and_41_out,
       and_42_out, and_43_out, and_44_out, and_45_out, and_46_out, and_47_out, and_48_out, and_49_out,
       and_50_out, and_51_out, and_52_out, and_53_out, and_54_out, and_55_out, and_56_out, and_57_out,
       and_58_out, and_59_out, and_60_out, and_61_out, and_62_out, and_63_out, and_64_out, and_65_out,
       and_66_out, and_67_out, and_68_out, and_69_out, and_70_out, and_71_out, and_72_out, and_73_out,
       and_74_out, and_75_out, and_76_out, and_77_out, and_78_out, and_79_out, and_80_out, and_81_out,
       and_82_out, and_83_out, and_84_out, and_85_out, and_86_out, and_87_out, and_88_out, and_89_out,
       and_90_out, and_91_out, and_92_out, and_93_out, and_94_out, and_95_out, and_96_out, and_97_out,
       and_98_out, and_99_out, and_100_out, and_101_out, and_102_out, and_103_out, and_104_out, and_105_out,
       and_106_out, and_107_out, and_108_out, and_109_out, not_1_out, not_2_out, not_3_out, not_4_out,
       not_5_out, not_6_out, not_7_out, not_8_out, not_9_out, not_10_out, not_11_out, not_12_out, not_13_out,
       not_14_out, not_15_out, not_16_out, not_17_out, not_18_out, or_1_out, or_2_out, or_3_out, or_4_out,
       or_5_out, or_6_out, or_7_out, or_8_out, or_9_out, or_10_out, or_11_out, or_12_out, or_13_out,
       or_14_out, or_15_out, or_16_out, or_17_out, or_18_out, or_19_out, or_20_out, or_21_out, or_22_out,
       or_23_out, or_24_out, or_25_out, or_26_out, or_27_out, or_28_out, or_29_out, or_30_out, or_31_out,
       or_32_out, or_33_out, or_34_out, or_35_out, or_36_out, or_37_out, or_38_out, or_39_out, or_40_out,
       or_41_out, or_42_out, or_43_out, or_44_out, or_45_out, xor_1_out, xor_2_out, xor_3_out, xor_4_out,
       xor_5_out, xor_6_out, xor_7_out, xor_8_out, xor_9_out, xor_10_out, xor_11_out, xor_12_out, xor_13_out,
       xor_14_out, xor_15_out, xor_16_out, xor_17_out, xor_18_out, xor_19_out, xor_20_out, xor_21_out,
       xor_22_out, xor_23_out, xor_24_out, xor_25_out, xor_26_out, xor_27_out, xor_28_out, xor_29_out,
       xor_30_out, xor_31_out, xor_32_out, xor_33_out, xor_34_out, xor_35_out, xor_36_out, xor_37_out,
       xor_38_out, xor_39_out, xor_40_out, xor_41_out, xor_42_out, xor_43_out, xor_44_out, xor_45_out,
       xor_46_out, xor_47_out, xor_48_out, xor_49_out, xor_50_out, xor_51_out, xor_52_out, xor_53_out,
       xor_54_out, xor_55_out, xor_56_out, xor_57_out, xor_58_out, xor_59_out, xor_60_out, xor_61_out,
       xor_62_out, xor_63_out;

  not not_1 (not_1_out, ZX);
  not not_2 (not_2_out, ZY);
  and and_1 (and_1_out, not_1_out, X0);
  and and_2 (and_2_out, not_1_out, X1);
  and and_3 (and_3_out, not_1_out, X2);
  and and_4 (and_4_out, not_1_out, X3);
  and and_5 (and_5_out, not_1_out, X4);
  and and_6 (and_6_out, not_1_out, X5);
  and and_7 (and_7_out, not_1_out, X6);
  and and_8 (and_8_out, not_1_out, X7);
  and and_9 (and_9_out, not_1_out, X8);
  and and_10 (and_10_out, not_1_out, X9);
  and and_11 (and_11_out, not_1_out, X10);
  and and_12 (and_12_out, not_1_out, X11);
  and and_13 (and_13_out, not_1_out, X12);
  and and_14 (and_14_out, not_1_out, X13);
  and and_15 (and_15_out, not_1_out, X14);
  and and_16 (and_16_out, not_1_out, X15);
  and and_17 (and_17_out, not_2_out, Y0);
  and and_18 (and_18_out, not_2_out, Y1);
  and and_19 (and_19_out, not_2_out, Y2);
  and and_20 (and_20_out, not_2_out, Y3);
  and and_21 (and_21_out, not_2_out, Y4);
  and and_22 (and_22_out, not_2_out, Y5);
  and and_23 (and_23_out, not_2_out, Y6);
  and and_24 (and_24_out, not_2_out, Y7);
  and and_25 (and_25_out, not_2_out, Y8);
  and and_26 (and_26_out, not_2_out, Y9);
  and and_27 (and_27_out, not_2_out, Y10);
  and and_28 (and_28_out, not_2_out, Y11);
  and and_29 (and_29_out, not_2_out, Y12);
  and and_30 (and_30_out, not_2_out, Y13);
  and and_31 (and_31_out, not_2_out, Y14);
  and and_32 (and_32_out, not_2_out, Y15);
  xor xor_1 (xor_1_out, NX, and_1_out);
  xor xor_2 (xor_2_out, NX, and_2_out);
  xor xor_3 (xor_3_out, NX, and_3_out);
  xor xor_4 (xor_4_out, NX, and_4_out);
  xor xor_5 (xor_5_out, NX, and_5_out);
  xor xor_6 (xor_6_out, NX, and_6_out);
  xor xor_7 (xor_7_out, NX, and_7_out);
  xor xor_8 (xor_8_out, NX, and_8_out);
  xor xor_9 (xor_9_out, NX, and_9_out);
  xor xor_10 (xor_10_out, NX, and_10_out);
  xor xor_11 (xor_11_out, NX, and_11_out);
  xor xor_12 (xor_12_out, NX, and_12_out);
  xor xor_13 (xor_13_out, NX, and_13_out);
  xor xor_14 (xor_14_out, NX, and_14_out);
  xor xor_15 (xor_15_out, NX, and_15_out);
  xor xor_16 (xor_16_out, NX, and_16_out);
  xor xor_17 (xor_17_out, NY, and_17_out);
  xor xor_18 (xor_18_out, NY, and_18_out);
  xor xor_19 (xor_19_out, NY, and_19_out);
  xor xor_20 (xor_20_out, NY, and_20_out);
  xor xor_21 (xor_21_out, NY, and_21_out);
  xor xor_22 (xor_22_out, NY, and_22_out);
  xor xor_23 (xor_23_out, NY, and_23_out);
  xor xor_24 (xor_24_out, NY, and_24_out);
  xor xor_25 (xor_25_out, NY, and_25_out);
  xor xor_26 (xor_26_out, NY, and_26_out);
  xor xor_27 (xor_27_out, NY, and_27_out);
  xor xor_28 (xor_28_out, NY, and_28_out);
  xor xor_29 (xor_29_out, NY, and_29_out);
  xor xor_30 (xor_30_out, NY, and_30_out);
  xor xor_31 (xor_31_out, NY, and_31_out);
  xor xor_32 (xor_32_out, NY, and_32_out);
  and and_33 (and_33_out, xor_1_out, xor_17_out);
  and and_34 (and_34_out, xor_2_out, xor_18_out);
  and and_35 (and_35_out, xor_3_out, xor_19_out);
  and and_36 (and_36_out, xor_4_out, xor_20_out);
  and and_37 (and_37_out, xor_5_out, xor_21_out);
  and and_38 (and_38_out, xor_6_out, xor_22_out);
  and and_39 (and_39_out, xor_7_out, xor_23_out);
  and and_40 (and_40_out, xor_8_out, xor_24_out);
  and and_41 (and_41_out, xor_9_out, xor_25_out);
  and and_42 (and_42_out, xor_10_out, xor_26_out);
  and and_43 (and_43_out, xor_11_out, xor_27_out);
  and and_44 (and_44_out, xor_12_out, xor_28_out);
  and and_45 (and_45_out, xor_13_out, xor_29_out);
  and and_46 (and_46_out, xor_14_out, xor_30_out);
  and and_47 (and_47_out, xor_15_out, xor_31_out);
  and and_48 (and_48_out, xor_16_out, xor_32_out);
  xor xor_33 (xor_33_out, xor_2_out, xor_18_out);
  xor xor_34 (xor_34_out, xor_3_out, xor_19_out);
  xor xor_35 (xor_35_out, xor_4_out, xor_20_out);
  xor xor_36 (xor_36_out, xor_5_out, xor_21_out);
  xor xor_37 (xor_37_out, xor_6_out, xor_22_out);
  xor xor_38 (xor_38_out, xor_7_out, xor_23_out);
  xor xor_39 (xor_39_out, xor_8_out, xor_24_out);
  xor xor_40 (xor_40_out, xor_9_out, xor_25_out);
  xor xor_41 (xor_41_out, xor_10_out, xor_26_out);
  xor xor_42 (xor_42_out, xor_11_out, xor_27_out);
  xor xor_43 (xor_43_out, xor_12_out, xor_28_out);
  xor xor_44 (xor_44_out, xor_13_out, xor_29_out);
  xor xor_45 (xor_45_out, xor_14_out, xor_30_out);
  xor xor_46 (xor_46_out, xor_15_out, xor_31_out);
  xor xor_47 (xor_47_out, xor_16_out, xor_32_out);
  and and_49 (and_49_out, xor_1_out, xor_17_out);
  xor xor_48 (xor_48_out, xor_1_out, xor_17_out);
  xor xor_49 (xor_49_out, and_49_out, xor_33_out);
  and and_50 (and_50_out, and_49_out, xor_33_out);
  and and_51 (and_51_out, xor_2_out, xor_18_out);
  xor xor_50 (xor_50_out, or_1_out, xor_34_out);
  and and_52 (and_52_out, or_1_out, xor_34_out);
  and and_53 (and_53_out, xor_3_out, xor_19_out);
  xor xor_51 (xor_51_out, or_2_out, xor_35_out);
  and and_54 (and_54_out, or_2_out, xor_35_out);
  and and_55 (and_55_out, xor_4_out, xor_20_out);
  xor xor_52 (xor_52_out, or_3_out, xor_36_out);
  and and_56 (and_56_out, or_3_out, xor_36_out);
  and and_57 (and_57_out, xor_5_out, xor_21_out);
  xor xor_53 (xor_53_out, or_4_out, xor_37_out);
  and and_58 (and_58_out, or_4_out, xor_37_out);
  and and_59 (and_59_out, xor_6_out, xor_22_out);
  xor xor_54 (xor_54_out, or_5_out, xor_38_out);
  and and_60 (and_60_out, or_5_out, xor_38_out);
  and and_61 (and_61_out, xor_7_out, xor_23_out);
  xor xor_55 (xor_55_out, or_6_out, xor_39_out);
  and and_62 (and_62_out, or_6_out, xor_39_out);
  and and_63 (and_63_out, xor_8_out, xor_24_out);
  xor xor_56 (xor_56_out, or_7_out, xor_40_out);
  and and_64 (and_64_out, or_7_out, xor_40_out);
  and and_65 (and_65_out, xor_9_out, xor_25_out);
  xor xor_57 (xor_57_out, or_8_out, xor_41_out);
  and and_66 (and_66_out, or_8_out, xor_41_out);
  and and_67 (and_67_out, xor_10_out, xor_26_out);
  xor xor_58 (xor_58_out, or_9_out, xor_42_out);
  and and_68 (and_68_out, or_9_out, xor_42_out);
  and and_69 (and_69_out, xor_11_out, xor_27_out);
  xor xor_59 (xor_59_out, or_10_out, xor_43_out);
  and and_70 (and_70_out, or_10_out, xor_43_out);
  and and_71 (and_71_out, xor_12_out, xor_28_out);
  xor xor_60 (xor_60_out, or_11_out, xor_44_out);
  and and_72 (and_72_out, or_11_out, xor_44_out);
  and and_73 (and_73_out, xor_13_out, xor_29_out);
  xor xor_61 (xor_61_out, or_12_out, xor_45_out);
  and and_74 (and_74_out, or_12_out, xor_45_out);
  and and_75 (and_75_out, xor_14_out, xor_30_out);
  xor xor_62 (xor_62_out, or_13_out, xor_46_out);
  and and_76 (and_76_out, or_13_out, xor_46_out);
  and and_77 (and_77_out, xor_15_out, xor_31_out);
  xor xor_63 (xor_63_out, or_14_out, xor_47_out);
  or or_1 (or_1_out, and_50_out, and_51_out);
  or or_2 (or_2_out, and_52_out, and_53_out);
  or or_3 (or_3_out, and_54_out, and_55_out);
  or or_4 (or_4_out, and_56_out, and_57_out);
  or or_5 (or_5_out, and_58_out, and_59_out);
  or or_6 (or_6_out, and_60_out, and_61_out);
  or or_7 (or_7_out, and_62_out, and_63_out);
  or or_8 (or_8_out, and_64_out, and_65_out);
  or or_9 (or_9_out, and_66_out, and_67_out);
  or or_10 (or_10_out, and_68_out, and_69_out);
  or or_11 (or_11_out, and_70_out, and_71_out);
  or or_12 (or_12_out, and_72_out, and_73_out);
  or or_13 (or_13_out, and_74_out, and_75_out);
  or or_14 (or_14_out, and_76_out, and_77_out);
  and and_78 (and_78_out, F, xor_48_out);
  not not_3 (not_3_out, F);
  and and_79 (and_79_out, not_3_out, and_33_out);
  and and_80 (and_80_out, F, xor_49_out);
  not not_4 (not_4_out, F);
  and and_81 (and_81_out, not_4_out, and_34_out);
  and and_82 (and_82_out, F, xor_50_out);
  not not_5 (not_5_out, F);
  and and_83 (and_83_out, not_5_out, and_35_out);
  and and_84 (and_84_out, F, xor_51_out);
  not not_6 (not_6_out, F);
  and and_85 (and_85_out, not_6_out, and_36_out);
  and and_86 (and_86_out, F, xor_52_out);
  not not_7 (not_7_out, F);
  and and_87 (and_87_out, not_7_out, and_37_out);
  and and_88 (and_88_out, F, xor_53_out);
  not not_8 (not_8_out, F);
  and and_89 (and_89_out, not_8_out, and_38_out);
  and and_90 (and_90_out, F, xor_54_out);
  not not_9 (not_9_out, F);
  and and_91 (and_91_out, not_9_out, and_39_out);
  and and_92 (and_92_out, F, xor_55_out);
  not not_10 (not_10_out, F);
  and and_93 (and_93_out, not_10_out, and_40_out);
  and and_94 (and_94_out, F, xor_56_out);
  not not_11 (not_11_out, F);
  and and_95 (and_95_out, not_11_out, and_41_out);
  and and_96 (and_96_out, F, xor_57_out);
  not not_12 (not_12_out, F);
  and and_97 (and_97_out, not_12_out, and_42_out);
  and and_98 (and_98_out, F, xor_58_out);
  not not_13 (not_13_out, F);
  and and_99 (and_99_out, not_13_out, and_43_out);
  and and_100 (and_100_out, F, xor_59_out);
  not not_14 (not_14_out, F);
  and and_101 (and_101_out, not_14_out, and_44_out);
  and and_102 (and_102_out, F, xor_60_out);
  not not_15 (not_15_out, F);
  and and_103 (and_103_out, not_15_out, and_45_out);
  and and_104 (and_104_out, F, xor_61_out);
  not not_16 (not_16_out, F);
  and and_105 (and_105_out, not_16_out, and_46_out);
  and and_106 (and_106_out, F, xor_62_out);
  not not_17 (not_17_out, F);
  and and_107 (and_107_out, not_17_out, and_47_out);
  and and_108 (and_108_out, F, xor_63_out);
  not not_18 (not_18_out, F);
  and and_109 (and_109_out, not_18_out, and_48_out);
  or or_15 (or_15_out, and_78_out, and_79_out);
  or or_16 (or_16_out, and_80_out, and_81_out);
  or or_17 (or_17_out, and_82_out, and_83_out);
  or or_18 (or_18_out, and_84_out, and_85_out);
  or or_19 (or_19_out, and_86_out, and_87_out);
  or or_20 (or_20_out, and_88_out, and_89_out);
  or or_21 (or_21_out, and_90_out, and_91_out);
  or or_22 (or_22_out, and_92_out, and_93_out);
  or or_23 (or_23_out, and_94_out, and_95_out);
  or or_24 (or_24_out, and_96_out, and_97_out);
  or or_25 (or_25_out, and_98_out, and_99_out);
  or or_26 (or_26_out, and_100_out, and_101_out);
  or or_27 (or_27_out, and_102_out, and_103_out);
  or or_28 (or_28_out, and_104_out, and_105_out);
  or or_29 (or_29_out, and_106_out, and_107_out);
  or or_30 (or_30_out, and_108_out, and_109_out);
  xor xor_64 (O0, NO, or_15_out);
  xor xor_65 (O1, NO, or_16_out);
  xor xor_66 (O2, NO, or_17_out);
  xor xor_67 (O3, NO, or_18_out);
  xor xor_68 (O4, NO, or_19_out);
  xor xor_69 (O5, NO, or_20_out);
  xor xor_70 (O6, NO, or_21_out);
  xor xor_71 (O7, NO, or_22_out);
  xor xor_72 (O8, NO, or_23_out);
  xor xor_73 (O9, NO, or_24_out);
  xor xor_74 (O10, NO, or_25_out);
  xor xor_75 (O11, NO, or_26_out);
  xor xor_76 (O12, NO, or_27_out);
  xor xor_77 (O13, NO, or_28_out);
  xor xor_78 (O14, NO, or_29_out);
  xor xor_79 (NG, NO, or_30_out);
  or or_31 (or_31_out, O0, O1);
  or or_32 (or_32_out, O2, O3);
  or or_33 (or_33_out, O4, O5);
  or or_34 (or_34_out, O6, O7);
  or or_35 (or_35_out, O8, O9);
  or or_36 (or_36_out, O10, O11);
  or or_37 (or_37_out, O12, O13);
  or or_38 (or_38_out, O14, NG);
  or or_39 (or_39_out, or_31_out, or_32_out);
  or or_40 (or_40_out, or_33_out, or_34_out);
  or or_41 (or_41_out, or_35_out, or_36_out);
  or or_42 (or_42_out, or_37_out, or_38_out);
  or or_43 (or_43_out, or_39_out, or_40_out);
  or or_44 (or_44_out, or_41_out, or_42_out);
  or or_45 (or_45_out, or_43_out, or_44_out);
  not not_19 (ZR, or_45_out);

  assign O15 = NG;
endmodule
