// Logisim project 16-bit 64 VRAM.circ as structural Verilog: 1 circuit, main circuit main
module main (
  input  in_1,
  input  in_2,
  input  in_3,
  input  in_4,
  input  in_5,
  input  in_6,
  input  in_7,
  input  in_8,
  input  in_9,
  input  in_10,
  input  in_11,
  input  in_12,
  input  in_13,
  input  in_14,
  input  in_15,
  input  in_16,
  input  in_17,
  input  in_18,
  input  in_19,
  input  in_20,
  input  in_21,
  input  in_22,
  input  in_23,
  output [31:0] out_24,
  output [31:0] out_25,
  output [31:0] out_26,
  output [31:0] out_27,
  output [31:0] out_28,
  output [31:0] out_29,
  output [31:0] out_30,
  output [31:0] out_31,
  output [31:0] out_32,
  output [31:0] out_33,
  output [31:0] out_34,
  output [31:0] out_35,
  output [31:0] out_36,
  output [31:0] out_37,
  output [31:0] out_38,
  output [31:0] out_39,
  output [31:0] out_40,
  output [31:0] out_41,
  output [31:0] out_42,
  output [31:0] out_43,
  output out_44,
  output out_45,
  output out_46,
  output out_47,
  output out_48,
  output out_49,
  output out_50,
  output out_51,
  output out_52,
  output out_53,
  output out_54,
  output out_55,
  output out_56,
  output out_57,
  output out_58,
  output out_59,
  output [31:0] out_60,
  output [31:0] out_61,
  output [31:0] out_62,
  output [31:0] out_63,
  output [31:0] out_64,
  output [31:0] out_65,
  output [31:0] out_66,
  output [31:0] out_67,
  output [31:0] out_68,
  output [31:0] out_69,
  output [31:0] out_70,
  output [31:0] out_71
);

  wire and_1_out, and_2_out, and_3_out, and_4_out, and_5_out, and_6_out, and_7_out, and_8_out, and_9_out,
       and_10_out, and_11_out, and_12_out, and_13_out, and_14_out, and_15_out, and_17_out, and_19_out,
       and_29_out, and_31_out, and_33_out, and_35_out, and_37_out, not_1_out, not_2_out, not_3_out,
       not_4_out, not_5_out, not_6_out, not_7_out, not_8_out, not_9_out, not_10_out;
  wire [15:0] and_21_out, and_22_out, and_23_out, and_24_out, and_25_out, and_26_out, and_27_out, and_28_out,
       main_1_out_26, main_2_out_26, main_3_out_26, main_4_out_26, main_5_out_26, main_6_out_26,
       main_7_out_26, main_8_out_26;
  wire [15:15] and_16_out, and_18_out, and_20_out, and_30_out, and_32_out, and_34_out, and_36_out, and_38_out;

  and and_1 (and_1_out, in_1, not_1_out);
  not not_1 (not_1_out, in_2);
  and and_2 (and_2_out, in_1, in_2);
  and and_3 (and_3_out, and_1_out, not_2_out);
  not not_2 (not_2_out, in_3);
  and and_4 (and_4_out, and_1_out, in_3);
  and and_5 (and_5_out, and_2_out, not_3_out);
  not not_3 (not_3_out, in_3);
  and and_6 (and_6_out, and_2_out, in_3);
  and and_7 (and_7_out, and_3_out, not_4_out);
  not not_4 (not_4_out, in_4);
  and and_8 (and_8_out, and_3_out, in_4);
  and and_9 (and_9_out, and_4_out, not_5_out);
  not not_5 (not_5_out, in_4);
  and and_10 (and_10_out, and_4_out, in_4);
  and and_11 (and_11_out, and_5_out, not_6_out);
  not not_6 (not_6_out, in_4);
  and and_12 (and_12_out, and_5_out, in_4);
  and and_13 (and_13_out, and_6_out, not_7_out);
  not not_7 (not_7_out, in_4);
  and and_14 (and_14_out, and_6_out, in_4);
  _16_bit_8_VRAM_main main_1 (
    .in_1(and_7_out), .in_2(in_5), .in_3(in_6), .in_4(in_7), .in_5(in_8), .in_6(in_9), .in_7(in_10),
    .in_8(in_11), .in_9(in_12), .in_10(in_13), .in_11(in_14), .in_12(in_15), .in_13(in_16), .in_14(in_17),
    .in_15(in_18), .in_16(in_19), .in_17(in_20), .in_18(in_21), .in_19(in_22), .in_20(in_23),
    .out_21(out_24[31:16]), .out_22(out_24[15:0]), .out_23(out_25[31:16]), .out_24(out_25[15:0]),
    .out_25(out_26[31:16]), .out_42(out_26[15:0]), .out_43(out_27[31:16]), .out_44(out_27[15:0]),
    .out_26(main_1_out_26[0]), .out_27(main_1_out_26[1]), .out_28(main_1_out_26[2]),
    .out_29(main_1_out_26[3]), .out_30(main_1_out_26[4]), .out_31(main_1_out_26[5]),
    .out_32(main_1_out_26[6]), .out_33(main_1_out_26[7]), .out_34(main_1_out_26[8]),
    .out_35(main_1_out_26[9]), .out_36(main_1_out_26[10]), .out_37(main_1_out_26[11]),
    .out_38(main_1_out_26[12]), .out_39(main_1_out_26[13]), .out_40(main_1_out_26[14]),
    .out_41(main_1_out_26[15]));
  _16_bit_8_VRAM_main main_2 (
    .in_1(and_8_out), .in_2(in_5), .in_3(in_6), .in_4(in_7), .in_5(in_8), .in_6(in_9), .in_7(in_10),
    .in_8(in_11), .in_9(in_12), .in_10(in_13), .in_11(in_14), .in_12(in_15), .in_13(in_16), .in_14(in_17),
    .in_15(in_18), .in_16(in_19), .in_17(in_20), .in_18(in_21), .in_19(in_22), .in_20(in_23),
    .out_21(out_28[31:16]), .out_22(out_28[15:0]), .out_23(out_29[31:16]), .out_24(out_29[15:0]),
    .out_25(out_30[31:16]), .out_42(out_30[15:0]), .out_43(out_31[31:16]), .out_44(out_31[15:0]),
    .out_26(main_2_out_26[0]), .out_27(main_2_out_26[1]), .out_28(main_2_out_26[2]),
    .out_29(main_2_out_26[3]), .out_30(main_2_out_26[4]), .out_31(main_2_out_26[5]),
    .out_32(main_2_out_26[6]), .out_33(main_2_out_26[7]), .out_34(main_2_out_26[8]),
    .out_35(main_2_out_26[9]), .out_36(main_2_out_26[10]), .out_37(main_2_out_26[11]),
    .out_38(main_2_out_26[12]), .out_39(main_2_out_26[13]), .out_40(main_2_out_26[14]),
    .out_41(main_2_out_26[15]));
  _16_bit_8_VRAM_main main_3 (
    .in_1(and_9_out), .in_2(in_5), .in_3(in_6), .in_4(in_7), .in_5(in_8), .in_6(in_9), .in_7(in_10),
    .in_8(in_11), .in_9(in_12), .in_10(in_13), .in_11(in_14), .in_12(in_15), .in_13(in_16), .in_14(in_17),
    .in_15(in_18), .in_16(in_19), .in_17(in_20), .in_18(in_21), .in_19(in_22), .in_20(in_23),
    .out_21(out_32[31:16]), .out_22(out_32[15:0]), .out_23(out_33[31:16]), .out_24(out_33[15:0]),
    .out_25(out_34[31:16]), .out_42(out_34[15:0]), .out_43(out_35[31:16]), .out_44(out_35[15:0]),
    .out_26(main_3_out_26[0]), .out_27(main_3_out_26[1]), .out_28(main_3_out_26[2]),
    .out_29(main_3_out_26[3]), .out_30(main_3_out_26[4]), .out_31(main_3_out_26[5]),
    .out_32(main_3_out_26[6]), .out_33(main_3_out_26[7]), .out_34(main_3_out_26[8]),
    .out_35(main_3_out_26[9]), .out_36(main_3_out_26[10]), .out_37(main_3_out_26[11]),
    .out_38(main_3_out_26[12]), .out_39(main_3_out_26[13]), .out_40(main_3_out_26[14]),
    .out_41(main_3_out_26[15]));
  _16_bit_8_VRAM_main main_4 (
    .in_1(and_10_out), .in_2(in_5), .in_3(in_6), .in_4(in_7), .in_5(in_8), .in_6(in_9), .in_7(in_10),
    .in_8(in_11), .in_9(in_12), .in_10(in_13), .in_11(in_14), .in_12(in_15), .in_13(in_16), .in_14(in_17),
    .in_15(in_18), .in_16(in_19), .in_17(in_20), .in_18(in_21), .in_19(in_22), .in_20(in_23),
    .out_21(out_36[31:16]), .out_22(out_36[15:0]), .out_23(out_37[31:16]), .out_24(out_37[15:0]),
    .out_25(out_38[31:16]), .out_42(out_38[15:0]), .out_43(out_39[31:16]), .out_44(out_39[15:0]),
    .out_26(main_4_out_26[0]), .out_27(main_4_out_26[1]), .out_28(main_4_out_26[2]),
    .out_29(main_4_out_26[3]), .out_30(main_4_out_26[4]), .out_31(main_4_out_26[5]),
    .out_32(main_4_out_26[6]), .out_33(main_4_out_26[7]), .out_34(main_4_out_26[8]),
    .out_35(main_4_out_26[9]), .out_36(main_4_out_26[10]), .out_37(main_4_out_26[11]),
    .out_38(main_4_out_26[12]), .out_39(main_4_out_26[13]), .out_40(main_4_out_26[14]),
    .out_41(main_4_out_26[15]));
  _16_bit_8_VRAM_main main_5 (
    .in_1(and_11_out), .in_2(in_5), .in_3(in_6), .in_4(in_7), .in_5(in_8), .in_6(in_9), .in_7(in_10),
    .in_8(in_11), .in_9(in_12), .in_10(in_13), .in_11(in_14), .in_12(in_15), .in_13(in_16), .in_14(in_17),
    .in_15(in_18), .in_16(in_19), .in_17(in_20), .in_18(in_21), .in_19(in_22), .in_20(in_23),
    .out_21(out_40[31:16]), .out_22(out_40[15:0]), .out_23(out_41[31:16]), .out_24(out_41[15:0]),
    .out_25(out_42[31:16]), .out_42(out_42[15:0]), .out_43(out_43[31:16]), .out_44(out_43[15:0]),
    .out_26(main_5_out_26[0]), .out_27(main_5_out_26[1]), .out_28(main_5_out_26[2]),
    .out_29(main_5_out_26[3]), .out_30(main_5_out_26[4]), .out_31(main_5_out_26[5]),
    .out_32(main_5_out_26[6]), .out_33(main_5_out_26[7]), .out_34(main_5_out_26[8]),
    .out_35(main_5_out_26[9]), .out_36(main_5_out_26[10]), .out_37(main_5_out_26[11]),
    .out_38(main_5_out_26[12]), .out_39(main_5_out_26[13]), .out_40(main_5_out_26[14]),
    .out_41(main_5_out_26[15]));
  _16_bit_8_VRAM_main main_6 (
    .in_1(and_12_out), .in_2(in_5), .in_3(in_6), .in_4(in_7), .in_5(in_8), .in_6(in_9), .in_7(in_10),
    .in_8(in_11), .in_9(in_12), .in_10(in_13), .in_11(in_14), .in_12(in_15), .in_13(in_16), .in_14(in_17),
    .in_15(in_18), .in_16(in_19), .in_17(in_20), .in_18(in_21), .in_19(in_22), .in_20(in_23),
    .out_21(out_60[31:16]), .out_22(out_60[15:0]), .out_23(out_61[31:16]), .out_24(out_61[15:0]),
    .out_25(out_62[31:16]), .out_42(out_62[15:0]), .out_43(out_63[31:16]), .out_44(out_63[15:0]),
    .out_26(main_6_out_26[0]), .out_27(main_6_out_26[1]), .out_28(main_6_out_26[2]),
    .out_29(main_6_out_26[3]), .out_30(main_6_out_26[4]), .out_31(main_6_out_26[5]),
    .out_32(main_6_out_26[6]), .out_33(main_6_out_26[7]), .out_34(main_6_out_26[8]),
    .out_35(main_6_out_26[9]), .out_36(main_6_out_26[10]), .out_37(main_6_out_26[11]),
    .out_38(main_6_out_26[12]), .out_39(main_6_out_26[13]), .out_40(main_6_out_26[14]),
    .out_41(main_6_out_26[15]));
  _16_bit_8_VRAM_main main_7 (
    .in_1(and_13_out), .in_2(in_5), .in_3(in_6), .in_4(in_7), .in_5(in_8), .in_6(in_9), .in_7(in_10),
    .in_8(in_11), .in_9(in_12), .in_10(in_13), .in_11(in_14), .in_12(in_15), .in_13(in_16), .in_14(in_17),
    .in_15(in_18), .in_16(in_19), .in_17(in_20), .in_18(in_21), .in_19(in_22), .in_20(in_23),
    .out_21(out_64[31:16]), .out_22(out_64[15:0]), .out_23(out_65[31:16]), .out_24(out_65[15:0]),
    .out_25(out_66[31:16]), .out_42(out_66[15:0]), .out_43(out_67[31:16]), .out_44(out_67[15:0]),
    .out_26(main_7_out_26[0]), .out_27(main_7_out_26[1]), .out_28(main_7_out_26[2]),
    .out_29(main_7_out_26[3]), .out_30(main_7_out_26[4]), .out_31(main_7_out_26[5]),
    .out_32(main_7_out_26[6]), .out_33(main_7_out_26[7]), .out_34(main_7_out_26[8]),
    .out_35(main_7_out_26[9]), .out_36(main_7_out_26[10]), .out_37(main_7_out_26[11]),
    .out_38(main_7_out_26[12]), .out_39(main_7_out_26[13]), .out_40(main_7_out_26[14]),
    .out_41(main_7_out_26[15]));
  _16_bit_8_VRAM_main main_8 (
    .in_1(and_14_out), .in_2(in_5), .in_3(in_6), .in_4(in_7), .in_5(in_8), .in_6(in_9), .in_7(in_10),
    .in_8(in_11), .in_9(in_12), .in_10(in_13), .in_11(in_14), .in_12(in_15), .in_13(in_16), .in_14(in_17),
    .in_15(in_18), .in_16(in_19), .in_17(in_20), .in_18(in_21), .in_19(in_22), .in_20(in_23),
    .out_21(out_68[31:16]), .out_22(out_68[15:0]), .out_23(out_69[31:16]), .out_24(out_69[15:0]),
    .out_25(out_70[31:16]), .out_42(out_70[15:0]), .out_43(out_71[31:16]), .out_44(out_71[15:0]),
    .out_26(main_8_out_26[0]), .out_27(main_8_out_26[1]), .out_28(main_8_out_26[2]),
    .out_29(main_8_out_26[3]), .out_30(main_8_out_26[4]), .out_31(main_8_out_26[5]),
    .out_32(main_8_out_26[6]), .out_33(main_8_out_26[7]), .out_34(main_8_out_26[8]),
    .out_35(main_8_out_26[9]), .out_36(main_8_out_26[10]), .out_37(main_8_out_26[11]),
    .out_38(main_8_out_26[12]), .out_39(main_8_out_26[13]), .out_40(main_8_out_26[14]),
    .out_41(main_8_out_26[15]));
  not not_8 (not_8_out, in_2);
  not not_9 (not_9_out, in_3);
  and and_15 (and_15_out, not_8_out, not_9_out);
  not not_10 (not_10_out, in_4);
  and and_16 (and_16_out[15], and_15_out, not_10_out);
  and and_17 (and_17_out, not_8_out, not_9_out);
  and and_18 (and_18_out[15], and_17_out, in_4);
  and and_19 (and_19_out, not_8_out, in_3);
  and and_20 (and_20_out[15], and_19_out, not_10_out);
  assign and_21_out = {16{and_16_out[15]}} & main_1_out_26;  // AND_Gate and_21, 16 bits wide
  assign and_22_out = {16{and_18_out[15]}} & main_2_out_26;  // AND_Gate and_22, 16 bits wide
  assign and_23_out = {16{and_20_out[15]}} & main_3_out_26;  // AND_Gate and_23, 16 bits wide
  assign and_24_out = {16{and_30_out[15]}} & main_4_out_26;  // AND_Gate and_24, 16 bits wide
  assign and_25_out = {16{and_32_out[15]}} & main_5_out_26;  // AND_Gate and_25, 16 bits wide
  assign and_26_out = {16{and_34_out[15]}} & main_6_out_26;  // AND_Gate and_26, 16 bits wide
  assign and_27_out = {16{and_36_out[15]}} & main_7_out_26;  // AND_Gate and_27, 16 bits wide
  assign and_28_out = {16{and_38_out[15]}} & main_8_out_26;  // AND_Gate and_28, 16 bits wide
  and and_29 (and_29_out, not_8_out, in_3);
  and and_30 (and_30_out[15], and_29_out, in_4);
  and and_31 (and_31_out, in_2, not_9_out);
  and and_32 (and_32_out[15], and_31_out, not_10_out);
  and and_33 (and_33_out, in_2, not_9_out);
  and and_34 (and_34_out[15], and_33_out, in_4);
  assign {out_59, out_58, out_57, out_56, out_55, out_54, out_53, out_52, out_51, out_50, out_49, out_48, out_47, out_46, out_45, out_44} = and_21_out | and_22_out | and_23_out | and_24_out | and_25_out | and_26_out | and_27_out | and_28_out;  // OR_Gate or_1, 16 bits wide
  and and_35 (and_35_out, in_2, in_3);
  and and_36 (and_36_out[15], and_35_out, not_10_out);
  and and_37 (and_37_out, in_2, in_3);
  and and_38 (and_38_out[15], and_37_out, in_4);

  // Notes on the sheet:
  //   Address
  //   DMux
  //   Output
  //   Decoder
endmodule
