// Logisim project 16-bit 8 RAM.circ as structural Verilog: 1 circuit, main circuit main
module main (
  input  in_1,
  input  in_2,
  input  in_3,
  input  in_4,
  input  in_5,
  input  in_6,
  input  in_7,
  input  in_8,
  input  in_9,
  input  in_10,
  input  in_11,
  input  in_12,
  input  in_13,
  input  in_14,
  input  in_15,
  input  in_16,
  input  in_17,
  input  in_18,
  input  in_19,
  input  in_20,
  output out_21,
  output out_22,
  output out_23,
  output out_24,
  output out_25,
  output out_26,
  output out_27,
  output out_28,
  output out_29,
  output out_30,
  output out_31,
  output out_32,
  output out_33,
  output out_34,
  output out_35,
  output out_36
);

  wire and_1_out, and_2_out, and_3_out, and_4_out, and_5_out, and_6_out, and_7_out, and_8_out, and_9_out,
       and_10_out, and_11_out, and_12_out, and_13_out, and_14_out, and_15_out, and_17_out, and_19_out,
       and_21_out, and_31_out, and_33_out, and_35_out, and_37_out, not_1_out, not_2_out, not_3_out,
       not_4_out, not_5_out, not_6_out, not_7_out, not_8_out, not_9_out, not_10_out;
  wire [15:0] and_23_out, and_24_out, and_25_out, and_26_out, and_27_out, and_28_out, and_29_out, and_30_out,
       main_1_out_33, main_2_out_33, main_3_out_33, main_4_out_33, main_5_out_33, main_6_out_33,
       main_7_out_33, main_8_out_33;
  wire [15:15] and_16_out, and_18_out, and_20_out, and_22_out, and_32_out, and_34_out, and_36_out, and_38_out;

  not not_1 (not_1_out, in_2);
  and and_1 (and_1_out, in_1, not_1_out);
  and and_2 (and_2_out, in_1, in_2);
  not not_2 (not_2_out, in_3);
  not not_3 (not_3_out, in_3);
  and and_3 (and_3_out, and_1_out, not_2_out);
  and and_4 (and_4_out, and_1_out, in_3);
  and and_5 (and_5_out, and_2_out, not_3_out);
  and and_6 (and_6_out, and_2_out, in_3);
  not not_4 (not_4_out, in_4);
  not not_5 (not_5_out, in_4);
  not not_6 (not_6_out, in_4);
  not not_7 (not_7_out, in_4);
  and and_7 (and_7_out, and_3_out, not_4_out);
  and and_8 (and_8_out, and_3_out, in_4);
  and and_9 (and_9_out, and_4_out, not_5_out);
  and and_10 (and_10_out, and_4_out, in_4);
  and and_11 (and_11_out, and_5_out, not_6_out);
  and and_12 (and_12_out, and_5_out, in_4);
  and and_13 (and_13_out, and_6_out, not_7_out);
  and and_14 (and_14_out, and_6_out, in_4);
  _16_bit_register_main main_1 (
    .in_2(in_5), .in_3(in_6), .in_4(in_7), .in_5(in_8), .in_6(in_9), .in_7(in_10), .in_8(in_11),
    .in_9(in_12), .in_10(in_13), .in_11(in_14), .in_12(in_15), .in_13(in_16), .in_14(in_17), .in_15(in_18),
    .in_16(in_19), .in_17(in_20), .out_18(main_1_out_33[15]), .out_19(main_1_out_33[14]),
    .out_20(main_1_out_33[13]), .out_21(main_1_out_33[12]), .out_22(main_1_out_33[11]),
    .out_23(main_1_out_33[10]), .out_24(main_1_out_33[9]), .out_25(main_1_out_33[8]),
    .out_26(main_1_out_33[7]), .out_27(main_1_out_33[6]), .out_28(main_1_out_33[5]),
    .out_29(main_1_out_33[4]), .out_30(main_1_out_33[3]), .out_31(main_1_out_33[2]),
    .out_32(main_1_out_33[1]), .out_33(main_1_out_33[0]), .in_1(and_7_out));
  _16_bit_register_main main_2 (
    .in_2(in_5), .in_3(in_6), .in_4(in_7), .in_5(in_8), .in_6(in_9), .in_7(in_10), .in_8(in_11),
    .in_9(in_12), .in_10(in_13), .in_11(in_14), .in_12(in_15), .in_13(in_16), .in_14(in_17), .in_15(in_18),
    .in_16(in_19), .in_17(in_20), .out_18(main_2_out_33[15]), .out_19(main_2_out_33[14]),
    .out_20(main_2_out_33[13]), .out_21(main_2_out_33[12]), .out_22(main_2_out_33[11]),
    .out_23(main_2_out_33[10]), .out_24(main_2_out_33[9]), .out_25(main_2_out_33[8]),
    .out_26(main_2_out_33[7]), .out_27(main_2_out_33[6]), .out_28(main_2_out_33[5]),
    .out_29(main_2_out_33[4]), .out_30(main_2_out_33[3]), .out_31(main_2_out_33[2]),
    .out_32(main_2_out_33[1]), .out_33(main_2_out_33[0]), .in_1(and_8_out));
  _16_bit_register_main main_3 (
    .in_2(in_5), .in_3(in_6), .in_4(in_7), .in_5(in_8), .in_6(in_9), .in_7(in_10), .in_8(in_11),
    .in_9(in_12), .in_10(in_13), .in_11(in_14), .in_12(in_15), .in_13(in_16), .in_14(in_17), .in_15(in_18),
    .in_16(in_19), .in_17(in_20), .out_18(main_3_out_33[15]), .out_19(main_3_out_33[14]),
    .out_20(main_3_out_33[13]), .out_21(main_3_out_33[12]), .out_22(main_3_out_33[11]),
    .out_23(main_3_out_33[10]), .out_24(main_3_out_33[9]), .out_25(main_3_out_33[8]),
    .out_26(main_3_out_33[7]), .out_27(main_3_out_33[6]), .out_28(main_3_out_33[5]),
    .out_29(main_3_out_33[4]), .out_30(main_3_out_33[3]), .out_31(main_3_out_33[2]),
    .out_32(main_3_out_33[1]), .out_33(main_3_out_33[0]), .in_1(and_9_out));
  _16_bit_register_main main_4 (
    .in_2(in_5), .in_3(in_6), .in_4(in_7), .in_5(in_8), .in_6(in_9), .in_7(in_10), .in_8(in_11),
    .in_9(in_12), .in_10(in_13), .in_11(in_14), .in_12(in_15), .in_13(in_16), .in_14(in_17), .in_15(in_18),
    .in_16(in_19), .in_17(in_20), .out_18(main_4_out_33[15]), .out_19(main_4_out_33[14]),
    .out_20(main_4_out_33[13]), .out_21(main_4_out_33[12]), .out_22(main_4_out_33[11]),
    .out_23(main_4_out_33[10]), .out_24(main_4_out_33[9]), .out_25(main_4_out_33[8]),
    .out_26(main_4_out_33[7]), .out_27(main_4_out_33[6]), .out_28(main_4_out_33[5]),
    .out_29(main_4_out_33[4]), .out_30(main_4_out_33[3]), .out_31(main_4_out_33[2]),
    .out_32(main_4_out_33[1]), .out_33(main_4_out_33[0]), .in_1(and_10_out));
  _16_bit_register_main main_5 (
    .in_2(in_5), .in_3(in_6), .in_4(in_7), .in_5(in_8), .in_6(in_9), .in_7(in_10), .in_8(in_11),
    .in_9(in_12), .in_10(in_13), .in_11(in_14), .in_12(in_15), .in_13(in_16), .in_14(in_17), .in_15(in_18),
    .in_16(in_19), .in_17(in_20), .out_18(main_5_out_33[15]), .out_19(main_5_out_33[14]),
    .out_20(main_5_out_33[13]), .out_21(main_5_out_33[12]), .out_22(main_5_out_33[11]),
    .out_23(main_5_out_33[10]), .out_24(main_5_out_33[9]), .out_25(main_5_out_33[8]),
    .out_26(main_5_out_33[7]), .out_27(main_5_out_33[6]), .out_28(main_5_out_33[5]),
    .out_29(main_5_out_33[4]), .out_30(main_5_out_33[3]), .out_31(main_5_out_33[2]),
    .out_32(main_5_out_33[1]), .out_33(main_5_out_33[0]), .in_1(and_11_out));
  _16_bit_register_main main_6 (
    .in_2(in_5), .in_3(in_6), .in_4(in_7), .in_5(in_8), .in_6(in_9), .in_7(in_10), .in_8(in_11),
    .in_9(in_12), .in_10(in_13), .in_11(in_14), .in_12(in_15), .in_13(in_16), .in_14(in_17), .in_15(in_18),
    .in_16(in_19), .in_17(in_20), .out_18(main_6_out_33[15]), .out_19(main_6_out_33[14]),
    .out_20(main_6_out_33[13]), .out_21(main_6_out_33[12]), .out_22(main_6_out_33[11]),
    .out_23(main_6_out_33[10]), .out_24(main_6_out_33[9]), .out_25(main_6_out_33[8]),
    .out_26(main_6_out_33[7]), .out_27(main_6_out_33[6]), .out_28(main_6_out_33[5]),
    .out_29(main_6_out_33[4]), .out_30(main_6_out_33[3]), .out_31(main_6_out_33[2]),
    .out_32(main_6_out_33[1]), .out_33(main_6_out_33[0]), .in_1(and_12_out));
  _16_bit_register_main main_7 (
    .in_2(in_5), .in_3(in_6), .in_4(in_7), .in_5(in_8), .in_6(in_9), .in_7(in_10), .in_8(in_11),
    .in_9(in_12), .in_10(in_13), .in_11(in_14), .in_12(in_15), .in_13(in_16), .in_14(in_17), .in_15(in_18),
    .in_16(in_19), .in_17(in_20), .out_18(main_7_out_33[15]), .out_19(main_7_out_33[14]),
    .out_20(main_7_out_33[13]), .out_21(main_7_out_33[12]), .out_22(main_7_out_33[11]),
    .out_23(main_7_out_33[10]), .out_24(main_7_out_33[9]), .out_25(main_7_out_33[8]),
    .out_26(main_7_out_33[7]), .out_27(main_7_out_33[6]), .out_28(main_7_out_33[5]),
    .out_29(main_7_out_33[4]), .out_30(main_7_out_33[3]), .out_31(main_7_out_33[2]),
    .out_32(main_7_out_33[1]), .out_33(main_7_out_33[0]), .in_1(and_13_out));
  _16_bit_register_main main_8 (
    .in_2(in_5), .in_3(in_6), .in_4(in_7), .in_5(in_8), .in_6(in_9), .in_7(in_10), .in_8(in_11),
    .in_9(in_12), .in_10(in_13), .in_11(in_14), .in_12(in_15), .in_13(in_16), .in_14(in_17), .in_15(in_18),
    .in_16(in_19), .in_17(in_20), .out_18(main_8_out_33[15]), .out_19(main_8_out_33[14]),
    .out_20(main_8_out_33[13]), .out_21(main_8_out_33[12]), .out_22(main_8_out_33[11]),
    .out_23(main_8_out_33[10]), .out_24(main_8_out_33[9]), .out_25(main_8_out_33[8]),
    .out_26(main_8_out_33[7]), .out_27(main_8_out_33[6]), .out_28(main_8_out_33[5]),
    .out_29(main_8_out_33[4]), .out_30(main_8_out_33[3]), .out_31(main_8_out_33[2]),
    .out_32(main_8_out_33[1]), .out_33(main_8_out_33[0]), .in_1(and_14_out));
  not not_8 (not_8_out, in_3);
  not not_9 (not_9_out, in_2);
  and and_15 (and_15_out, not_9_out, not_8_out);
  and and_16 (and_16_out[15], and_15_out, not_10_out);
  and and_17 (and_17_out, not_9_out, not_8_out);
  not not_10 (not_10_out, in_4);
  and and_18 (and_18_out[15], and_17_out, in_4);
  and and_19 (and_19_out, not_9_out, in_3);
  and and_20 (and_20_out[15], and_19_out, not_10_out);
  and and_21 (and_21_out, not_9_out, in_3);
  and and_22 (and_22_out[15], and_21_out, in_4);
  assign and_23_out = {16{and_16_out[15]}} & main_1_out_33;  // AND_Gate and_23, 16 bits wide
  assign and_24_out = {16{and_18_out[15]}} & main_2_out_33;  // AND_Gate and_24, 16 bits wide
  assign and_25_out = {16{and_20_out[15]}} & main_3_out_33;  // AND_Gate and_25, 16 bits wide
  assign and_26_out = {16{and_22_out[15]}} & main_4_out_33;  // AND_Gate and_26, 16 bits wide
  assign and_27_out = {16{and_32_out[15]}} & main_5_out_33;  // AND_Gate and_27, 16 bits wide
  assign and_28_out = {16{and_34_out[15]}} & main_6_out_33;  // AND_Gate and_28, 16 bits wide
  assign and_29_out = {16{and_36_out[15]}} & main_7_out_33;  // AND_Gate and_29, 16 bits wide
  assign and_30_out = {16{and_38_out[15]}} & main_8_out_33;  // AND_Gate and_30, 16 bits wide
  and and_31 (and_31_out, in_2, not_8_out);
  and and_32 (and_32_out[15], and_31_out, not_10_out);
  and and_33 (and_33_out, in_2, not_8_out);
  and and_34 (and_34_out[15], and_33_out, in_4);
  and and_35 (and_35_out, in_2, in_3);
  and and_36 (and_36_out[15], and_35_out, not_10_out);
  assign {out_21, out_22, out_23, out_24, out_25, out_26, out_27, out_28, out_29, out_30, out_31, out_32, out_33, out_34, out_35, out_36} = and_23_out | and_24_out | and_25_out | and_26_out | and_27_out | and_28_out | and_29_out | and_30_out;  // OR_Gate or_1, 16 bits wide
  and and_37 (and_37_out, in_2, in_3);
  and and_38 (and_38_out[15], and_37_out, in_4);

  // Notes on the sheet:
  //   Address
  //   Input
  //   DMux
  //   Output
  //   Decoder
endmodule
