// Logisim project 16-bit 8 VRAM.circ as structural Verilog: 1 circuit, main circuit main
module main (
  input  in_1,
  input  in_2,
  input  in_3,
  input  in_4,
  input  in_5,
  input  in_6,
  input  in_7,
  input  in_8,
  input  in_9,
  input  in_10,
  input  in_11,
  input  in_12,
  input  in_13,
  input  in_14,
  input  in_15,
  input  in_16,
  input  in_17,
  input  in_18,
  input  in_19,
  input  in_20,
  output [15:0] out_21,
  output [15:0] out_22,
  output [15:0] out_23,
  output [15:0] out_24,
  output [15:0] out_25,
  output out_26,
  output out_27,
  output out_28,
  output out_29,
  output out_30,
  output out_31,
  output out_32,
  output out_33,
  output out_34,
  output out_35,
  output out_36,
  output out_37,
  output out_38,
  output out_39,
  output out_40,
  output out_41,
  output [15:0] out_42,
  output [15:0] out_43,
  output [15:0] out_44
);

  wire and_1_out, and_2_out, and_3_out, and_4_out, and_5_out, and_6_out, and_7_out, and_8_out, and_9_out,
       and_10_out, and_11_out, and_12_out, and_13_out, and_14_out, and_15_out, and_16_out, and_18_out,
       and_20_out, and_30_out, and_32_out, and_34_out, and_36_out, not_1_out, not_2_out, not_3_out,
       not_4_out, not_5_out, not_6_out, not_7_out, not_8_out, not_9_out, not_10_out;
  wire [15:0] and_22_out, and_23_out, and_24_out, and_25_out, and_26_out, and_27_out, and_28_out, and_29_out;
  wire [15:15] and_17_out, and_19_out, and_21_out, and_31_out, and_33_out, and_35_out, and_37_out, and_38_out;

  not not_1 (not_1_out, in_2);
  and and_1 (and_1_out, in_1, not_1_out);
  and and_2 (and_2_out, in_1, in_2);
  not not_2 (not_2_out, in_3);
  not not_3 (not_3_out, in_3);
  and and_3 (and_3_out, and_1_out, not_2_out);
  and and_4 (and_4_out, and_1_out, in_3);
  and and_5 (and_5_out, and_2_out, not_3_out);
  and and_6 (and_6_out, and_2_out, in_3);
  not not_4 (not_4_out, in_4);
  not not_5 (not_5_out, in_4);
  not not_6 (not_6_out, in_4);
  not not_7 (not_7_out, in_4);
  and and_7 (and_7_out, and_3_out, not_4_out);
  and and_8 (and_8_out, and_3_out, in_4);
  and and_9 (and_9_out, and_4_out, not_5_out);
  and and_10 (and_10_out, and_4_out, in_4);
  and and_11 (and_11_out, and_5_out, not_6_out);
  and and_12 (and_12_out, and_5_out, in_4);
  and and_13 (and_13_out, and_6_out, not_7_out);
  and and_14 (and_14_out, and_6_out, in_4);
  _16_bit_register_main main_1 (
    .in_2(in_5), .in_3(in_6), .in_4(in_7), .in_5(in_8), .in_6(in_9), .in_7(in_10), .in_8(in_11),
    .in_9(in_12), .in_10(in_13), .in_11(in_14), .in_12(in_15), .in_13(in_16), .in_14(in_17), .in_15(in_18),
    .in_16(in_19), .in_17(in_20), .out_18(out_21[15]), .out_19(out_21[14]), .out_20(out_21[13]),
    .out_21(out_21[12]), .out_22(out_21[11]), .out_23(out_21[10]), .out_24(out_21[9]), .out_25(out_21[8]),
    .out_26(out_21[7]), .out_27(out_21[6]), .out_28(out_21[5]), .out_29(out_21[4]), .out_30(out_21[3]),
    .out_31(out_21[2]), .out_32(out_21[1]), .out_33(out_21[0]), .in_1(and_7_out));
  _16_bit_register_main main_2 (
    .in_2(in_5), .in_3(in_6), .in_4(in_7), .in_5(in_8), .in_6(in_9), .in_7(in_10), .in_8(in_11),
    .in_9(in_12), .in_10(in_13), .in_11(in_14), .in_12(in_15), .in_13(in_16), .in_14(in_17), .in_15(in_18),
    .in_16(in_19), .in_17(in_20), .out_18(out_22[15]), .out_19(out_22[14]), .out_20(out_22[13]),
    .out_21(out_22[12]), .out_22(out_22[11]), .out_23(out_22[10]), .out_24(out_22[9]), .out_25(out_22[8]),
    .out_26(out_22[7]), .out_27(out_22[6]), .out_28(out_22[5]), .out_29(out_22[4]), .out_30(out_22[3]),
    .out_31(out_22[2]), .out_32(out_22[1]), .out_33(out_22[0]), .in_1(and_8_out));
  _16_bit_register_main main_3 (
    .in_2(in_5), .in_3(in_6), .in_4(in_7), .in_5(in_8), .in_6(in_9), .in_7(in_10), .in_8(in_11),
    .in_9(in_12), .in_10(in_13), .in_11(in_14), .in_12(in_15), .in_13(in_16), .in_14(in_17), .in_15(in_18),
    .in_16(in_19), .in_17(in_20), .out_18(out_23[15]), .out_19(out_23[14]), .out_20(out_23[13]),
    .out_21(out_23[12]), .out_22(out_23[11]), .out_23(out_23[10]), .out_24(out_23[9]), .out_25(out_23[8]),
    .out_26(out_23[7]), .out_27(out_23[6]), .out_28(out_23[5]), .out_29(out_23[4]), .out_30(out_23[3]),
    .out_31(out_23[2]), .out_32(out_23[1]), .out_33(out_23[0]), .in_1(and_9_out));
  _16_bit_register_main main_4 (
    .in_2(in_5), .in_3(in_6), .in_4(in_7), .in_5(in_8), .in_6(in_9), .in_7(in_10), .in_8(in_11),
    .in_9(in_12), .in_10(in_13), .in_11(in_14), .in_12(in_15), .in_13(in_16), .in_14(in_17), .in_15(in_18),
    .in_16(in_19), .in_17(in_20), .out_18(out_24[15]), .out_19(out_24[14]), .out_20(out_24[13]),
    .out_21(out_24[12]), .out_22(out_24[11]), .out_23(out_24[10]), .out_24(out_24[9]), .out_25(out_24[8]),
    .out_26(out_24[7]), .out_27(out_24[6]), .out_28(out_24[5]), .out_29(out_24[4]), .out_30(out_24[3]),
    .out_31(out_24[2]), .out_32(out_24[1]), .out_33(out_24[0]), .in_1(and_10_out));
  _16_bit_register_main main_5 (
    .in_2(in_5), .in_3(in_6), .in_4(in_7), .in_5(in_8), .in_6(in_9), .in_7(in_10), .in_8(in_11),
    .in_9(in_12), .in_10(in_13), .in_11(in_14), .in_12(in_15), .in_13(in_16), .in_14(in_17), .in_15(in_18),
    .in_16(in_19), .in_17(in_20), .out_18(out_25[15]), .out_19(out_25[14]), .out_20(out_25[13]),
    .out_21(out_25[12]), .out_22(out_25[11]), .out_23(out_25[10]), .out_24(out_25[9]), .out_25(out_25[8]),
    .out_26(out_25[7]), .out_27(out_25[6]), .out_28(out_25[5]), .out_29(out_25[4]), .out_30(out_25[3]),
    .out_31(out_25[2]), .out_32(out_25[1]), .out_33(out_25[0]), .in_1(and_11_out));
  _16_bit_register_main main_6 (
    .in_2(in_5), .in_3(in_6), .in_4(in_7), .in_5(in_8), .in_6(in_9), .in_7(in_10), .in_8(in_11),
    .in_9(in_12), .in_10(in_13), .in_11(in_14), .in_12(in_15), .in_13(in_16), .in_14(in_17), .in_15(in_18),
    .in_16(in_19), .in_17(in_20), .out_18(out_42[15]), .out_19(out_42[14]), .out_20(out_42[13]),
    .out_21(out_42[12]), .out_22(out_42[11]), .out_23(out_42[10]), .out_24(out_42[9]), .out_25(out_42[8]),
    .out_26(out_42[7]), .out_27(out_42[6]), .out_28(out_42[5]), .out_29(out_42[4]), .out_30(out_42[3]),
    .out_31(out_42[2]), .out_32(out_42[1]), .out_33(out_42[0]), .in_1(and_12_out));
  _16_bit_register_main main_7 (
    .in_2(in_5), .in_3(in_6), .in_4(in_7), .in_5(in_8), .in_6(in_9), .in_7(in_10), .in_8(in_11),
    .in_9(in_12), .in_10(in_13), .in_11(in_14), .in_12(in_15), .in_13(in_16), .in_14(in_17), .in_15(in_18),
    .in_16(in_19), .in_17(in_20), .out_18(out_43[15]), .out_19(out_43[14]), .out_20(out_43[13]),
    .out_21(out_43[12]), .out_22(out_43[11]), .out_23(out_43[10]), .out_24(out_43[9]), .out_25(out_43[8]),
    .out_26(out_43[7]), .out_27(out_43[6]), .out_28(out_43[5]), .out_29(out_43[4]), .out_30(out_43[3]),
    .out_31(out_43[2]), .out_32(out_43[1]), .out_33(out_43[0]), .in_1(and_13_out));
  _16_bit_register_main main_8 (
    .in_2(in_5), .in_3(in_6), .in_4(in_7), .in_5(in_8), .in_6(in_9), .in_7(in_10), .in_8(in_11),
    .in_9(in_12), .in_10(in_13), .in_11(in_14), .in_12(in_15), .in_13(in_16), .in_14(in_17), .in_15(in_18),
    .in_16(in_19), .in_17(in_20), .out_18(out_44[15]), .out_19(out_44[14]), .out_20(out_44[13]),
    .out_21(out_44[12]), .out_22(out_44[11]), .out_23(out_44[10]), .out_24(out_44[9]), .out_25(out_44[8]),
    .out_26(out_44[7]), .out_27(out_44[6]), .out_28(out_44[5]), .out_29(out_44[4]), .out_30(out_44[3]),
    .out_31(out_44[2]), .out_32(out_44[1]), .out_33(out_44[0]), .in_1(and_14_out));
  not not_8 (not_8_out, in_2);
  and and_15 (and_15_out, not_8_out, not_9_out);
  not not_9 (not_9_out, in_3);
  and and_16 (and_16_out, not_8_out, not_9_out);
  not not_10 (not_10_out, in_4);
  and and_17 (and_17_out[15], and_15_out, not_10_out);
  and and_18 (and_18_out, not_8_out, in_3);
  and and_19 (and_19_out[15], and_16_out, in_4);
  and and_20 (and_20_out, not_8_out, in_3);
  and and_21 (and_21_out[15], and_18_out, not_10_out);
  assign and_22_out = {16{and_17_out[15]}} & out_21;  // AND_Gate and_22, 16 bits wide
  assign and_23_out = {16{and_19_out[15]}} & out_22;  // AND_Gate and_23, 16 bits wide
  assign and_24_out = {16{and_21_out[15]}} & out_23;  // AND_Gate and_24, 16 bits wide
  assign and_25_out = {16{and_31_out[15]}} & out_24;  // AND_Gate and_25, 16 bits wide
  assign and_26_out = {16{and_33_out[15]}} & out_25;  // AND_Gate and_26, 16 bits wide
  assign and_27_out = {16{and_35_out[15]}} & out_42;  // AND_Gate and_27, 16 bits wide
  assign and_28_out = {16{and_37_out[15]}} & out_43;  // AND_Gate and_28, 16 bits wide
  assign and_29_out = {16{and_38_out[15]}} & out_44;  // AND_Gate and_29, 16 bits wide
  and and_30 (and_30_out, in_2, not_9_out);
  and and_31 (and_31_out[15], and_20_out, in_4);
  and and_32 (and_32_out, in_2, not_9_out);
  and and_33 (and_33_out[15], and_30_out, not_10_out);
  and and_34 (and_34_out, in_2, in_3);
  and and_35 (and_35_out[15], and_32_out, in_4);
  assign {out_41, out_40, out_39, out_38, out_37, out_36, out_35, out_34, out_33, out_32, out_31, out_30, out_29, out_28, out_27, out_26} = and_22_out | and_23_out | and_24_out | and_25_out | and_26_out | and_27_out | and_28_out | and_29_out;  // OR_Gate or_1, 16 bits wide
  and and_36 (and_36_out, in_2, in_3);
  and and_37 (and_37_out[15], and_34_out, not_10_out);
  and and_38 (and_38_out[15], and_36_out, in_4);

  // Notes on the sheet:
  //   Address
  //   Input
  //   DMux
  //   Output
  //   Decoder
endmodule
