// Logisim project 16-bit PC.circ as structural Verilog
module main (
  input  load,
  input  inc,
  input  reset,
  input  IN15,
  input  IN14,
  input  IN13,
  input  IN12,
  input  IN11,
  input  IN10,
  input  IN9,
  input  IN8,
  input  IN7,
  input  IN6,
  input  IN5,
  input  IN4,
  input  IN3,
  input  IN2,
  input  IN1,
  input  IN0,
  output O15,
  output O14,
  output O13,
  output O12,
  output O11,
  output O10,
  output O9,
  output O8,
  output O7,
  output O6,
  output O5,
  output O4,
  output O3,
  output O2,
  output O1,
  output O0
);

  wire adder_1_cout, adder_1_out, adder_2_cout, adder_2_out, adder_3_cout, adder_3_out, adder_4_cout,
       adder_4_out, adder_5_cout, adder_5_out, adder_6_cout, adder_6_out, adder_7_cout, adder_7_out,
       adder_8_cout, adder_8_out, adder_9_cout, adder_9_out, adder_10_cout, adder_10_out, adder_11_cout,
       adder_11_out, adder_12_cout, adder_12_out, adder_13_cout, adder_13_out, adder_14_cout, adder_14_out,
       adder_15_cout, adder_15_out, adder_16_out, and_1_out, and_2_out, and_3_out, and_4_out, and_5_out,
       and_6_out, and_7_out, and_8_out, and_9_out, and_10_out, and_11_out, and_12_out, and_13_out,
       and_14_out, and_15_out, and_16_out, clock_1_out, multiplexer_1_out, multiplexer_2_out,
       multiplexer_3_out, multiplexer_4_out, multiplexer_5_out, multiplexer_6_out, multiplexer_7_out,
       multiplexer_8_out, multiplexer_9_out, multiplexer_10_out, multiplexer_11_out, multiplexer_12_out,
       multiplexer_13_out, multiplexer_14_out, multiplexer_15_out, multiplexer_16_out, not_1_out, not_2_out,
       not_3_out, not_4_out, not_5_out, not_6_out, not_7_out, not_8_out, not_9_out, not_10_out, not_11_out,
       not_12_out, not_13_out, not_14_out, not_15_out, not_16_out;

  Multiplexer #(.enable("false")) multiplexer_1 (.in0(adder_1_out), .in1(IN0), .out(multiplexer_1_out), .sel(load));
  Multiplexer #(.enable("false")) multiplexer_2 (.in0(adder_2_out), .in1(IN1), .out(multiplexer_2_out), .sel(load));
  Multiplexer #(.enable("false")) multiplexer_3 (.in0(adder_3_out), .in1(IN2), .out(multiplexer_3_out), .sel(load));
  Multiplexer #(.enable("false")) multiplexer_4 (.in0(adder_4_out), .in1(IN3), .out(multiplexer_4_out), .sel(load));
  Multiplexer #(.enable("false")) multiplexer_5 (.in0(adder_5_out), .in1(IN4), .out(multiplexer_5_out), .sel(load));
  Multiplexer #(.enable("false")) multiplexer_6 (.in0(adder_6_out), .in1(IN5), .out(multiplexer_6_out), .sel(load));
  Multiplexer #(.enable("false")) multiplexer_7 (.in0(adder_7_out), .in1(IN6), .out(multiplexer_7_out), .sel(load));
  Multiplexer #(.enable("false")) multiplexer_8 (.in0(adder_8_out), .in1(IN7), .out(multiplexer_8_out), .sel(load));
  Multiplexer #(.enable("false")) multiplexer_9 (.in0(adder_9_out), .in1(IN8), .out(multiplexer_9_out), .sel(load));
  Multiplexer #(.enable("false")) multiplexer_10 (.in0(adder_10_out), .in1(IN9), .out(multiplexer_10_out), .sel(load));
  Multiplexer #(.enable("false")) multiplexer_11 (.in0(adder_11_out), .in1(IN10), .out(multiplexer_11_out), .sel(load));
  Multiplexer #(.enable("false")) multiplexer_12 (.in0(adder_12_out), .in1(IN11), .out(multiplexer_12_out), .sel(load));
  Multiplexer #(.enable("false")) multiplexer_13 (.in0(adder_13_out), .in1(IN12), .out(multiplexer_13_out), .sel(load));
  Multiplexer #(.enable("false")) multiplexer_14 (.in0(adder_14_out), .in1(IN13), .out(multiplexer_14_out), .sel(load));
  Multiplexer #(.enable("false")) multiplexer_15 (.in0(adder_15_out), .in1(IN14), .out(multiplexer_15_out), .sel(load));
  Multiplexer #(.enable("false")) multiplexer_16 (.in0(adder_16_out), .in1(IN15), .out(multiplexer_16_out), .sel(load));
  Adder #(.width(1)) adder_1 (.a(O0), .b(inc), .out(adder_1_out), .cout(adder_1_cout));  // open: cin
  Adder #(.width(1)) adder_2 (.a(O1), .b(adder_1_cout), .out(adder_2_out), .cout(adder_2_cout));  // open: cin
  Adder #(.width(1)) adder_3 (.a(O2), .b(adder_2_cout), .out(adder_3_out), .cout(adder_3_cout));  // open: cin
  Adder #(.width(1)) adder_4 (.a(O3), .b(adder_3_cout), .out(adder_4_out), .cout(adder_4_cout));  // open: cin
  Adder #(.width(1)) adder_5 (.a(O4), .b(adder_4_cout), .out(adder_5_out), .cout(adder_5_cout));  // open: cin
  Adder #(.width(1)) adder_6 (.a(O5), .b(adder_5_cout), .out(adder_6_out), .cout(adder_6_cout));  // open: cin
  Adder #(.width(1)) adder_7 (.a(O6), .b(adder_6_cout), .out(adder_7_out), .cout(adder_7_cout));  // open: cin
  Adder #(.width(1)) adder_8 (.a(O7), .b(adder_7_cout), .out(adder_8_out), .cout(adder_8_cout));  // open: cin
  Adder #(.width(1)) adder_9 (.a(O8), .b(adder_8_cout), .out(adder_9_out), .cout(adder_9_cout));  // open: cin
  Adder #(.width(1)) adder_10 (.a(O9), .b(adder_9_cout), .out(adder_10_out), .cout(adder_10_cout));  // open: cin
  Adder #(.width(1)) adder_11 (.a(O10), .b(adder_10_cout), .out(adder_11_out), .cout(adder_11_cout));  // open: cin
  Adder #(.width(1)) adder_12 (.a(O11), .b(adder_11_cout), .out(adder_12_out), .cout(adder_12_cout));  // open: cin
  Adder #(.width(1)) adder_13 (.a(O12), .b(adder_12_cout), .out(adder_13_out), .cout(adder_13_cout));  // open: cin
  Adder #(.width(1)) adder_14 (.a(O13), .b(adder_13_cout), .out(adder_14_out), .cout(adder_14_cout));  // open: cin
  Adder #(.width(1)) adder_15 (.a(O14), .b(adder_14_cout), .out(adder_15_out), .cout(adder_15_cout));  // open: cin
  Adder #(.width(1)) adder_16 (.a(O15), .b(adder_15_cout), .out(adder_16_out));  // open: cin, cout
  not not_1 (not_1_out, reset);
  not not_2 (not_2_out, reset);
  not not_3 (not_3_out, reset);
  not not_4 (not_4_out, reset);
  not not_5 (not_5_out, reset);
  not not_6 (not_6_out, reset);
  not not_7 (not_7_out, reset);
  not not_8 (not_8_out, reset);
  not not_9 (not_9_out, reset);
  not not_10 (not_10_out, reset);
  not not_11 (not_11_out, reset);
  not not_12 (not_12_out, reset);
  not not_13 (not_13_out, reset);
  not not_14 (not_14_out, reset);
  not not_15 (not_15_out, reset);
  not not_16 (not_16_out, reset);
  and and_1 (and_1_out, multiplexer_1_out, not_1_out);
  and and_2 (and_2_out, multiplexer_2_out, not_2_out);
  and and_3 (and_3_out, multiplexer_3_out, not_3_out);
  and and_4 (and_4_out, multiplexer_4_out, not_4_out);
  and and_5 (and_5_out, multiplexer_5_out, not_5_out);
  and and_6 (and_6_out, multiplexer_6_out, not_6_out);
  and and_7 (and_7_out, multiplexer_7_out, not_7_out);
  and and_8 (and_8_out, multiplexer_8_out, not_8_out);
  and and_9 (and_9_out, multiplexer_9_out, not_9_out);
  and and_10 (and_10_out, multiplexer_10_out, not_10_out);
  and and_11 (and_11_out, multiplexer_11_out, not_11_out);
  and and_12 (and_12_out, multiplexer_12_out, not_12_out);
  and and_13 (and_13_out, multiplexer_13_out, not_13_out);
  and and_14 (and_14_out, multiplexer_14_out, not_14_out);
  and and_15 (and_15_out, multiplexer_15_out, not_15_out);
  and and_16 (and_16_out, multiplexer_16_out, not_16_out);
  Clock clock_1 (.out(clock_1_out));
  D_Flip_Flop d_ff_1 (.clk(clock_1_out), .D(and_1_out), .Q(O0));  // open: Qn, preset, en, reset
  D_Flip_Flop d_ff_2 (.clk(clock_1_out), .D(and_2_out), .Q(O1));  // open: Qn, preset, en, reset
  D_Flip_Flop d_ff_3 (.clk(clock_1_out), .D(and_3_out), .Q(O2));  // open: Qn, preset, en, reset
  D_Flip_Flop d_ff_4 (.clk(clock_1_out), .D(and_4_out), .Q(O3));  // open: Qn, preset, en, reset
  D_Flip_Flop d_ff_5 (.clk(clock_1_out), .D(and_5_out), .Q(O4));  // open: Qn, preset, en, reset
  D_Flip_Flop d_ff_6 (.clk(clock_1_out), .D(and_6_out), .Q(O5));  // open: Qn, preset, en, reset
  D_Flip_Flop d_ff_7 (.clk(clock_1_out), .D(and_7_out), .Q(O6));  // open: Qn, preset, en, reset
  D_Flip_Flop d_ff_8 (.clk(clock_1_out), .D(and_8_out), .Q(O7));  // open: Qn, preset, en, reset
  D_Flip_Flop d_ff_9 (.clk(clock_1_out), .D(and_9_out), .Q(O8));  // open: Qn, preset, en, reset
  D_Flip_Flop d_ff_10 (.clk(clock_1_out), .D(and_10_out), .Q(O9));  // open: Qn, preset, en, reset
  D_Flip_Flop d_ff_11 (.clk(clock_1_out), .D(and_11_out), .Q(O10));  // open: Qn, preset, en, reset
  D_Flip_Flop d_ff_12 (.clk(clock_1_out), .D(and_12_out), .Q(O11));  // open: Qn, preset, en, reset
  D_Flip_Flop d_ff_13 (.clk(clock_1_out), .D(and_13_out), .Q(O12));  // open: Qn, preset, en, reset
  D_Flip_Flop d_ff_14 (.clk(clock_1_out), .D(and_14_out), .Q(O13));  // open: Qn, preset, en, reset
  D_Flip_Flop d_ff_15 (.clk(clock_1_out), .D(and_15_out), .Q(O14));  // open: Qn, preset, en, reset
  D_Flip_Flop d_ff_16 (.clk(clock_1_out), .D(and_16_out), .Q(O15));  // open: Qn, preset, en, reset
endmodule
