// Logisim project 16-bit register.circ as structural Verilog
module main (
  input  in_1,
  input  in_2,
  input  in_3,
  input  in_4,
  input  in_5,
  input  in_6,
  input  in_7,
  input  in_8,
  input  in_9,
  input  in_10,
  input  in_11,
  input  in_12,
  input  in_13,
  input  in_14,
  input  in_15,
  input  in_16,
  input  in_17,
  output out_18,
  output out_19,
  output out_20,
  output out_21,
  output out_22,
  output out_23,
  output out_24,
  output out_25,
  output out_26,
  output out_27,
  output out_28,
  output out_29,
  output out_30,
  output out_31,
  output out_32,
  output out_33
);

  wire clock_1_out, multiplexer_1_out, multiplexer_2_out, multiplexer_3_out, multiplexer_4_out,
       multiplexer_5_out, multiplexer_6_out, multiplexer_7_out, multiplexer_8_out, multiplexer_9_out,
       multiplexer_10_out, multiplexer_11_out, multiplexer_12_out, multiplexer_13_out, multiplexer_14_out,
       multiplexer_15_out, multiplexer_16_out;

  Clock clock_1 (.out(clock_1_out));
  Multiplexer #(.enable("false")) multiplexer_1 (.in0(out_18), .in1(in_2), .out(multiplexer_1_out), .sel(in_1));
  Multiplexer #(.enable("false")) multiplexer_2 (.in0(out_19), .in1(in_3), .out(multiplexer_2_out), .sel(in_1));
  Multiplexer #(.enable("false")) multiplexer_3 (.in0(out_20), .in1(in_4), .out(multiplexer_3_out), .sel(in_1));
  Multiplexer #(.enable("false")) multiplexer_4 (.in0(out_21), .in1(in_5), .out(multiplexer_4_out), .sel(in_1));
  Multiplexer #(.enable("false")) multiplexer_5 (.in0(out_22), .in1(in_6), .out(multiplexer_5_out), .sel(in_1));
  Multiplexer #(.enable("false")) multiplexer_6 (.in0(out_23), .in1(in_7), .out(multiplexer_6_out), .sel(in_1));
  Multiplexer #(.enable("false")) multiplexer_7 (.in0(out_24), .in1(in_8), .out(multiplexer_7_out), .sel(in_1));
  Multiplexer #(.enable("false")) multiplexer_8 (.in0(out_25), .in1(in_9), .out(multiplexer_8_out), .sel(in_1));
  Multiplexer #(.enable("false")) multiplexer_9 (.in0(out_26), .in1(in_10), .out(multiplexer_9_out), .sel(in_1));
  Multiplexer #(.enable("false")) multiplexer_10 (.in0(out_27), .in1(in_11), .out(multiplexer_10_out), .sel(in_1));
  Multiplexer #(.enable("false")) multiplexer_11 (.in0(out_28), .in1(in_12), .out(multiplexer_11_out), .sel(in_1));
  Multiplexer #(.enable("false")) multiplexer_12 (.in0(out_29), .in1(in_13), .out(multiplexer_12_out), .sel(in_1));
  Multiplexer #(.enable("false")) multiplexer_13 (.in0(out_30), .in1(in_14), .out(multiplexer_13_out), .sel(in_1));
  Multiplexer #(.enable("false")) multiplexer_14 (.in0(out_31), .in1(in_15), .out(multiplexer_14_out), .sel(in_1));
  Multiplexer #(.enable("false")) multiplexer_15 (.in0(out_32), .in1(in_16), .out(multiplexer_15_out), .sel(in_1));
  Multiplexer #(.enable("false")) multiplexer_16 (.in0(out_33), .in1(in_17), .out(multiplexer_16_out), .sel(in_1));
  D_Flip_Flop d_ff_1 (.clk(clock_1_out), .D(multiplexer_1_out), .Q(out_18));  // open: Qn, preset, en, reset
  D_Flip_Flop d_ff_2 (.clk(clock_1_out), .D(multiplexer_2_out), .Q(out_19));  // open: Qn, preset, en, reset
  D_Flip_Flop d_ff_3 (.clk(clock_1_out), .D(multiplexer_3_out), .Q(out_20));  // open: Qn, preset, en, reset
  D_Flip_Flop d_ff_4 (.clk(clock_1_out), .D(multiplexer_4_out), .Q(out_21));  // open: Qn, preset, en, reset
  D_Flip_Flop d_ff_5 (.clk(clock_1_out), .D(multiplexer_5_out), .Q(out_22));  // open: Qn, preset, en, reset
  D_Flip_Flop d_ff_6 (.clk(clock_1_out), .D(multiplexer_6_out), .Q(out_23));  // open: Qn, preset, en, reset
  D_Flip_Flop d_ff_7 (.clk(clock_1_out), .D(multiplexer_7_out), .Q(out_24));  // open: Qn, preset, en, reset
  D_Flip_Flop d_ff_8 (.clk(clock_1_out), .D(multiplexer_8_out), .Q(out_25));  // open: Qn, preset, en, reset
  D_Flip_Flop d_ff_9 (.clk(clock_1_out), .D(multiplexer_9_out), .Q(out_26));  // open: Qn, preset, en, reset
  D_Flip_Flop d_ff_10 (.clk(clock_1_out), .D(multiplexer_10_out), .Q(out_27));  // open: Qn, preset, en, reset
  D_Flip_Flop d_ff_11 (.clk(clock_1_out), .D(multiplexer_11_out), .Q(out_28));  // open: Qn, preset, en, reset
  D_Flip_Flop d_ff_12 (.clk(clock_1_out), .D(multiplexer_12_out), .Q(out_29));  // open: Qn, preset, en, reset
  D_Flip_Flop d_ff_13 (.clk(clock_1_out), .D(multiplexer_13_out), .Q(out_30));  // open: Qn, preset, en, reset
  D_Flip_Flop d_ff_14 (.clk(clock_1_out), .D(multiplexer_14_out), .Q(out_31));  // open: Qn, preset, en, reset
  D_Flip_Flop d_ff_15 (.clk(clock_1_out), .D(multiplexer_15_out), .Q(out_32));  // open: Qn, preset, en, reset
  D_Flip_Flop d_ff_16 (.clk(clock_1_out), .D(multiplexer_16_out), .Q(out_33));  // open: Qn, preset, en, reset
endmodule
