// Logisim project 16-bit CPU.circ as structural Verilog: 1 circuit, main circuit main
module main (
  input  in_1,
  input  in_2,
  input  in_3,
  input  in_4,
  input  in_5,
  input  in_6,
  input  in_7,
  input  in_8,
  input  in_9,
  input  in_10,
  input  in_11,
  input  in_12,
  input  in_13,
  input  in_14,
  input  in_15,
  input  in_16,
  input  in_17,
  input  in_18,
  input  in_19,
  input  in_20,
  input  in_21,
  input  in_22,
  input  in_23,
  input  in_24,
  input  in_25,
  input  in_26,
  input  in_27,
  input  in_28,
  input  in_29,
  input  in_30,
  input  in_31,
  input  in_32,
  input  in_33,
  output out_34,
  output out_35,
  output out_36,
  output out_37,
  output out_38,
  output out_39,
  output OutM,
  output out_41,
  output out_42,
  output out_43,
  output out_44,
  output out_45,
  output out_46,
  output out_47,
  output out_48,
  output out_49,
  output WriteM,
  output out_51,
  output out_52,
  output out_53,
  output out_54,
  output out_55,
  output out_56,
  output out_57,
  output Address_RAM,
  output out_59,
  output out_60,
  output out_61,
  output out_62,
  output out_63,
  output out_64,
  output out_65,
  output out_66,
  output out_67,
  output out_68,
  output out_69,
  output out_70,
  output out_71,
  output out_72,
  output out_73,
  output Address_ROM,
  output out_75,
  output out_76,
  output out_77,
  output out_78,
  output out_79,
  output out_80,
  output out_81,
  output out_82
);

  wire and_3_out, and_6_out, and_7_out, and_8_out, and_9_out, B_out_18, B_out_19, B_out_20, B_out_21,
       B_out_22, B_out_23, B_out_24, B_out_25, B_out_26, B_out_27, B_out_28, B_out_29, B_out_30, B_out_31,
       B_out_32, B_out_33, main_2_p36, main_2_p38, not_2_out, not_4_out, not_5_out, or_2_out, or_4_out,
       or_5_out;
  wire [15:0] and_1_out, and_2_out, and_4_out, and_5_out, not_1_out, not_3_out, or_1_out, or_3_out;

  assign not_1_out = ~{16{in_1}};  // NOT_Gate not_1, 16 bits wide
  assign and_1_out = {out_34, out_35, out_36, out_37, out_38, out_39, OutM, out_41, out_42, out_43, out_44, out_45, out_46, out_47, out_48, out_49} & {16{in_1}};  // AND_Gate and_1, 16 bits wide
  assign and_2_out = {in_1, in_2, in_3, in_4, in_5, in_6, in_7, in_8, in_9, in_10, in_11, in_12, in_13, in_14, in_15, in_16} & not_1_out;  // AND_Gate and_2, 16 bits wide
  assign or_1_out = and_1_out | and_2_out;  // OR_Gate or_1, 16 bits wide
  not not_2 (not_2_out, in_1);
  or or_2 (or_2_out, not_2_out, in_11);
  _16_bit_register_main A (
    .in_2(or_1_out[15]), .in_3(or_1_out[14]), .in_4(or_1_out[13]), .in_5(or_1_out[12]), .in_6(or_1_out[11]),
    .in_7(or_1_out[10]), .in_8(or_1_out[9]), .in_9(or_1_out[8]), .in_10(or_1_out[7]), .in_11(or_1_out[6]),
    .in_12(or_1_out[5]), .in_13(or_1_out[4]), .in_14(or_1_out[3]), .in_15(or_1_out[2]), .in_16(or_1_out[1]),
    .in_17(or_1_out[0]), .out_18(out_51), .out_19(out_52), .out_20(out_53), .out_21(out_54), .out_22(out_55),
    .out_23(out_56), .out_24(out_57), .out_25(Address_RAM), .out_26(out_59), .out_27(out_60),
    .out_28(out_61), .out_29(out_62), .out_30(out_63), .out_31(out_64), .out_32(out_65), .out_33(out_66),
    .in_1(or_2_out));
  and and_3 (and_3_out, in_1, in_12);
  assign not_3_out = ~{16{in_4}};  // NOT_Gate not_3, 16 bits wide
  assign and_4_out = {out_51, out_52, out_53, out_54, out_55, out_56, out_57, Address_RAM, out_59, out_60, out_61, out_62, out_63, out_64, out_65, out_66} & not_3_out;  // AND_Gate and_4, 16 bits wide
  assign and_5_out = {in_17, in_18, in_19, in_20, in_21, in_22, in_23, in_24, in_25, in_26, in_27, in_28, in_29, in_30, in_31, in_32} & {16{in_4}};  // AND_Gate and_5, 16 bits wide
  _16_bit_register_main B (
    .in_2(out_34), .in_3(out_35), .in_4(out_36), .in_5(out_37), .in_6(out_38), .in_7(out_39), .in_8(OutM),
    .in_9(out_41), .in_10(out_42), .in_11(out_43), .in_12(out_44), .in_13(out_45), .in_14(out_46),
    .in_15(out_47), .in_16(out_48), .in_17(out_49), .out_18(B_out_18), .out_19(B_out_19), .out_20(B_out_20),
    .out_21(B_out_21), .out_22(B_out_22), .out_23(B_out_23), .out_24(B_out_24), .out_25(B_out_25),
    .out_26(B_out_26), .out_27(B_out_27), .out_28(B_out_28), .out_29(B_out_29), .out_30(B_out_30),
    .out_31(B_out_31), .out_32(B_out_32), .out_33(B_out_33), .in_1(and_3_out));
  assign or_3_out = and_4_out | and_5_out;  // OR_Gate or_3, 16 bits wide
  not not_4 (not_4_out, in_33);
  and and_6 (and_6_out, in_1, or_4_out);
  _16_bit_PC_main main_1 (
    .IN15(out_51), .IN14(out_52), .IN13(out_53), .IN12(out_54), .IN11(out_55), .IN10(out_56), .IN9(out_57),
    .IN8(Address_RAM), .IN7(out_59), .IN6(out_60), .IN5(out_61), .IN4(out_62), .IN3(out_63), .IN2(out_64),
    .IN1(out_65), .IN0(out_66), .O15(out_67), .O14(out_68), .O13(out_69), .O12(out_70), .O11(out_71),
    .O10(out_72), .O9(out_73), .O8(Address_ROM), .O7(out_75), .O6(out_76), .O5(out_77), .O4(out_78),
    .O3(out_79), .O2(out_80), .O1(out_81), .O0(out_82), .load(and_6_out), .inc(not_4_out), .reset(in_33));
  and and_7 (and_7_out, in_14, main_2_p38);
  and and_8 (and_8_out, in_15, main_2_p36);
  or or_4 (or_4_out, and_7_out, and_8_out, and_9_out);
  and and_9 (and_9_out, in_16, not_5_out);
  or or_5 (or_5_out, main_2_p36, main_2_p38);
  not not_5 (not_5_out, or_5_out);
  // _16_bit_ALU_final_main main_2: pin names not known; wires that end beside it: B_out_18, B_out_19, B_out_20, B_out_21, B_out_22, B_out_23, B_out_24, B_out_25, B_out_26, B_out_27, B_out_28, B_out_29, B_out_30, B_out_31, B_out_32, B_out_33, or_3_out[15], or_3_out[14], or_3_out[13], or_3_out[12], or_3_out[11], or_3_out[10], or_3_out[9], or_3_out[8], or_3_out[7], or_3_out[6], or_3_out[5], or_3_out[4], or_3_out[3], or_3_out[2], or_3_out[1], or_3_out[0], in_5, in_6, in_7, main_2_p36, in_8, main_2_p38, in_9, in_10, out_34, out_35, out_36, out_37, out_38, out_39, OutM, out_41, out_42, out_43, out_44, out_45, out_46, out_47, out_48, out_49
  and and_10 (WriteM, in_13, in_1);

  // Notes on the sheet:
  //   OP code
  //   OP code
  //   D1
  //   OP code
  //   a
  //   D2
  //   OP code
  //   J1
  //   J2
  //   J3
  //   ZR
  //   NG
  //   D3
  //   OP code
endmodule
