// Logisim project Hack computer.circ as structural Verilog: 1 circuit, main circuit main
module main (
);

  wire and_1_out, and_2_out, and_3_out, and_4_out, button_1_out, clock_1_out, main_1_writem, not_1_out,
       not_2_out, not_3_out, not_4_out, not_5_out, not_6_out, not_7_out;
  wire [6:0] keyboard_1_data;
  wire [14:0] main_1_out_66;
  wire [15:0] bit_extender_1_out, main_1_out_49, main_1_out_82, main_2_out_44, multiplexer_1_out,
       multiplexer_2_out, ram_1_data, rom_1_data;
  wire [31:0] main_2_out_24, main_2_out_25, main_2_out_26, main_2_out_27, main_2_out_28, main_2_out_29,
       main_2_out_30, main_2_out_31, main_2_out_32, main_2_out_33, main_2_out_34, main_2_out_35,
       main_2_out_36, main_2_out_37, main_2_out_38, main_2_out_39, main_2_out_40, main_2_out_41,
       main_2_out_42, main_2_out_43, main_2_out_60, main_2_out_61, main_2_out_62, main_2_out_63,
       main_2_out_64, main_2_out_65, main_2_out_66, main_2_out_67, main_2_out_68, main_2_out_69,
       main_2_out_70, main_2_out_71;

  Button button_1 (.out(button_1_out));
  not not_1 (not_1_out, button_1_out);
  ROM #(.addrWidth(16), .dataWidth(16)) rom_1 (.addr(main_1_out_82), .data(rom_1_data));  // open: sel
  not not_2 (not_2_out, not_1_out);
  _16_bit_CPU_main main_1 (
    .in_1(rom_1_data[15]), .in_2(rom_1_data[14]), .in_3(rom_1_data[13]), .in_4(rom_1_data[12]),
    .in_5(rom_1_data[11]), .in_6(rom_1_data[10]), .in_7(rom_1_data[9]), .in_8(rom_1_data[8]),
    .in_9(rom_1_data[7]), .in_10(rom_1_data[6]), .in_11(rom_1_data[5]), .in_12(rom_1_data[4]),
    .in_13(rom_1_data[3]), .in_14(rom_1_data[2]), .in_15(rom_1_data[1]), .in_16(rom_1_data[0]),
    .in_17(multiplexer_2_out[15]), .in_18(multiplexer_2_out[14]), .in_19(multiplexer_2_out[13]),
    .in_20(multiplexer_2_out[12]), .in_21(multiplexer_2_out[11]), .in_22(multiplexer_2_out[10]),
    .in_23(multiplexer_2_out[9]), .in_24(multiplexer_2_out[8]), .in_25(multiplexer_2_out[7]),
    .in_26(multiplexer_2_out[6]), .in_27(multiplexer_2_out[5]), .in_28(multiplexer_2_out[4]),
    .in_29(multiplexer_2_out[3]), .in_30(multiplexer_2_out[2]), .in_31(multiplexer_2_out[1]),
    .in_32(multiplexer_2_out[0]), .in_33(not_2_out), .out_34(main_1_out_49[15]), .out_35(main_1_out_49[14]),
    .out_36(main_1_out_49[13]), .out_37(main_1_out_49[12]), .out_38(main_1_out_49[11]),
    .out_39(main_1_out_49[10]), .OutM(main_1_out_49[9]), .out_41(main_1_out_49[8]),
    .out_42(main_1_out_49[7]), .out_43(main_1_out_49[6]), .out_44(main_1_out_49[5]),
    .out_45(main_1_out_49[4]), .out_46(main_1_out_49[3]), .out_47(main_1_out_49[2]),
    .out_48(main_1_out_49[1]), .out_49(main_1_out_49[0]), .WriteM(main_1_writem), .out_52(main_1_out_66[14]),
    .out_53(main_1_out_66[13]), .out_54(main_1_out_66[12]), .out_55(main_1_out_66[11]),
    .out_56(main_1_out_66[10]), .out_57(main_1_out_66[9]), .Address_RAM(main_1_out_66[8]),
    .out_59(main_1_out_66[7]), .out_60(main_1_out_66[6]), .out_61(main_1_out_66[5]),
    .out_62(main_1_out_66[4]), .out_63(main_1_out_66[3]), .out_64(main_1_out_66[2]),
    .out_65(main_1_out_66[1]), .out_66(main_1_out_66[0]), .out_67(main_1_out_82[15]),
    .out_68(main_1_out_82[14]), .out_69(main_1_out_82[13]), .out_70(main_1_out_82[12]),
    .out_71(main_1_out_82[11]), .out_72(main_1_out_82[10]), .out_73(main_1_out_82[9]),
    .Address_ROM(main_1_out_82[8]), .out_75(main_1_out_82[7]), .out_76(main_1_out_82[6]),
    .out_77(main_1_out_82[5]), .out_78(main_1_out_82[4]), .out_79(main_1_out_82[3]),
    .out_80(main_1_out_82[2]), .out_81(main_1_out_82[1]), .out_82(main_1_out_82[0]));  // open: out_51
  and and_1 (and_1_out, main_1_out_66[14], main_1_out_66[13], main_1_out_66[12], main_1_out_66[11], main_1_out_66[10], main_1_out_66[9], main_1_out_66[8], main_1_out_66[7], main_1_out_66[6], main_1_out_66[5], main_1_out_66[4], main_1_out_66[3], main_1_out_66[2], main_1_out_66[1], main_1_out_66[0]);
  not not_3 (not_3_out, and_1_out);
  and and_2 (and_2_out, main_1_out_66[14], main_1_out_66[13], main_1_out_66[12], main_1_out_66[11], main_1_out_66[10], main_1_out_66[9], main_1_out_66[8], main_1_out_66[7]);
  and and_3 (and_3_out, main_1_writem, not_3_out, not_4_out);
  not not_4 (not_4_out, and_2_out);
  and and_4 (and_4_out, main_1_writem, not_3_out, and_2_out);
  Keyboard #(.trigger("falling")) keyboard_1 (
    .clk(and_1_out), .re(not_1_out), .clr(not_5_out), .data(keyboard_1_data));  // open: avail
  not not_5 (not_5_out, not_1_out);
  RAM #(.addrWidth(15), .dataWidth(16), .bus("separate")) ram_1 (
    .addr(main_1_out_66), .din(main_1_out_49), .data(ram_1_data), .str(and_3_out), .sel(not_1_out),
    .clk(clock_1_out), .ld(not_1_out), .clr(not_6_out));
  not not_6 (not_6_out, not_1_out);
  Clock clock_1 (.out(clock_1_out));
  assign bit_extender_1_out = {{9{1'b0}}, keyboard_1_data};  // Bit_Extender bit_extender_1
  _16_bit_64_VRAM_main main_2 (
    .in_2(main_1_out_66[5]), .in_3(main_1_out_66[4]), .in_4(main_1_out_66[3]), .in_5(main_1_out_66[2]),
    .in_6(main_1_out_66[1]), .in_7(main_1_out_66[0]), .in_8(main_1_out_49[15]), .in_9(main_1_out_49[14]),
    .in_10(main_1_out_49[13]), .in_11(main_1_out_49[12]), .in_12(main_1_out_49[11]),
    .in_13(main_1_out_49[10]), .in_14(main_1_out_49[9]), .in_15(main_1_out_49[8]), .in_16(main_1_out_49[7]),
    .in_17(main_1_out_49[6]), .in_18(main_1_out_49[5]), .in_19(main_1_out_49[4]), .in_20(main_1_out_49[3]),
    .in_21(main_1_out_49[2]), .in_22(main_1_out_49[1]), .in_23(main_1_out_49[0]), .in_1(and_4_out),
    .out_24(main_2_out_24), .out_25(main_2_out_25), .out_26(main_2_out_26), .out_27(main_2_out_27),
    .out_28(main_2_out_28), .out_29(main_2_out_29), .out_30(main_2_out_30), .out_31(main_2_out_31),
    .out_32(main_2_out_32), .out_33(main_2_out_33), .out_34(main_2_out_34), .out_35(main_2_out_35),
    .out_36(main_2_out_36), .out_37(main_2_out_37), .out_38(main_2_out_38), .out_39(main_2_out_39),
    .out_40(main_2_out_40), .out_41(main_2_out_41), .out_42(main_2_out_42), .out_43(main_2_out_43),
    .out_60(main_2_out_60), .out_61(main_2_out_61), .out_62(main_2_out_62), .out_63(main_2_out_63),
    .out_64(main_2_out_64), .out_65(main_2_out_65), .out_66(main_2_out_66), .out_67(main_2_out_67),
    .out_68(main_2_out_68), .out_69(main_2_out_69), .out_70(main_2_out_70), .out_71(main_2_out_71),
    .out_44(main_2_out_44[0]), .out_45(main_2_out_44[1]), .out_46(main_2_out_44[2]),
    .out_47(main_2_out_44[3]), .out_48(main_2_out_44[4]), .out_49(main_2_out_44[5]),
    .out_50(main_2_out_44[6]), .out_51(main_2_out_44[7]), .out_52(main_2_out_44[8]),
    .out_53(main_2_out_44[9]), .out_54(main_2_out_44[10]), .out_55(main_2_out_44[11]),
    .out_56(main_2_out_44[12]), .out_57(main_2_out_44[13]), .out_58(main_2_out_44[14]),
    .out_59(main_2_out_44[15]));
  Multiplexer #(.width(16), .enable("false")) multiplexer_1 (
    .in0(ram_1_data), .in1(main_2_out_44), .out(multiplexer_1_out), .sel(and_2_out));
  not not_7 (not_7_out, and_1_out);
  Multiplexer #(.width(16), .enable("false")) multiplexer_2 (
    .in0(bit_extender_1_out), .in1(multiplexer_1_out), .out(multiplexer_2_out), .sel(not_7_out));
  DotMatrix #(.inputtype("row"), .matrixcols(32), .matrixrows(32)) dotmatrix_1 (
    .row0(main_2_out_24), .row1(main_2_out_25), .row2(main_2_out_26), .row3(main_2_out_27),
    .row4(main_2_out_28), .row5(main_2_out_29), .row6(main_2_out_30), .row7(main_2_out_31),
    .row8(main_2_out_32), .row9(main_2_out_33), .row10(main_2_out_34), .row11(main_2_out_35),
    .row12(main_2_out_36), .row13(main_2_out_37), .row14(main_2_out_38), .row15(main_2_out_39),
    .row16(main_2_out_40), .row17(main_2_out_41), .row18(main_2_out_42), .row19(main_2_out_43),
    .row20(main_2_out_60), .row21(main_2_out_61), .row22(main_2_out_62), .row23(main_2_out_63),
    .row24(main_2_out_64), .row25(main_2_out_65), .row26(main_2_out_66), .row27(main_2_out_67),
    .row28(main_2_out_68), .row29(main_2_out_69), .row30(main_2_out_70), .row31(main_2_out_71));

  // Notes on the sheet:
  //   ROM
  //   contents of rom_1 (hex, n*v repeats v):
  //   7fff fc10 6 e305 0 ea87 7f80 e308 0 ea87
  //   RAM
  //   Keybaord
  //   Adress MSB and second to it used to switch between RAM and VRAM
  //   32 x 32 Screen
endmodule
